// Logisim project RISC_V_32.circ as structural Verilog: 11 circuits, main circuit Microcontroller
module CPU (
  input  [31:0] juhis,
  input  [31:0] malu_sisend,
  input  reset,
  input  clk,
  input  [19:0] Ext_Interrupt,
  output [31:0] juhise_aadress,
  output [31:0] ALU_valjund,
  output kirjuta_mallu,
  output [31:0] malu_valjund
);

  wire and_1_out, and_2_out, and_3_out, and_4_out, and_5_out, and_6_out, and_7_out, and_8_out, and_9_out,
       and_10_out, and_11_out, and_12_out, and_13_out, and_14_out, and_15_out, and_16_out, and_17_out,
       and_18_out, and_19_out, and_20_out, and_21_out, and_22_out, and_23_out, and_24_out, and_25_out,
       and_26_out, and_27_out, and_28_out, and_29_out, and_30_out, and_31_out, and_32_out, and_33_out,
       and_34_out, comparator_1_eq, comparator_2_eq, comparator_3_eq, comparator_4_eq, comparator_5_eq,
       comparator_6_eq, comparator_7_eq, comparator_8_eq, instruction_decoder_1_alu_src_a,
       instruction_decoder_1_alu_src_b, instruction_decoder_1_branch_select,
       instruction_decoder_1_kehtiv_opcode, Katkestus, kirjutaCSR, MIE, mret, multiplexer_4_out, not_1_out,
       not_2_out, or_1_out, or_2_out, or_4_out, or_5_out, or_6_out, or_7_out, or_8_out, or_9_out, or_10_out,
       or_11_out, or_12_out, or_13_out, or_14_out, or_15_out, or_16_out, or_17_out, or_18_out, or_19_out,
       or_20_out, or_21_out, or_22_out, or_23_out, or_24_out, or_25_out, or_26_out, or_27_out, or_28_out,
       or_29_out, or_30_out, or_31_out, or_32_out, or_33_out, or_34_out, or_36_out, or_37_out, or_38_out,
       or_39_out, or_40_out, or_41_out, or_42_out, or_43_out, or_44_out, or_45_out, or_46_out, or_47_out,
       or_48_out, or_49_out, or_50_out, or_51_out, or_52_out, or_53_out, or_54_out, or_55_out, or_56_out,
       or_57_out, or_58_out, or_59_out, or_60_out, or_61_out, or_62_out, or_63_out, or_64_out, or_65_out,
       or_67_out, or_68_out, s_r_ff_1_q, s_r_ff_2_q, tundmatu_opcode, undriven, undriven_2, undriven_3, VJKA;
  wire [1:0] instruction_decoder_1_register_mux, not_5_out;
  wire [2:0] instruction_decoder_1_data_type, instruction_decoder_1_pc_controll;
  wire [3:0] multiplexer_8_out, shifter_1_out;
  wire [4:0] instruction_decoder_1_command, instruction_decoder_1_rd, instruction_decoder_1_rs1,
       instruction_decoder_1_rs2;
  wire [11:0] CSRaadress;
  wire [17:17] register_2_q_2;
  wire [29:0] register_1_q, register_2_q;
  wire [31:0] adder_1_out, and_35_out, bit_extender_1_out, bit_extender_2_out, bit_extender_3_out,
       bit_extender_4_out, controlled_buffer_1_out, controlled_buffer_32_out, counter_1_q, CSRvaljund,
       instruction_decoder_1_immidiate, KatkestuseAadress, multiplexer_2_out, multiplexer_3_out,
       multiplexer_5_out, multiplexer_6_out, multiplexer_7_out, multiplexer_9_out, multiplexer_10_out,
       multiplexer_11_out, multiplexer_12_out, not_4_out, or_69_out, registers_1_register_output_1,
       registers_1_register_output_2, shifter_2_out, shifter_3_out, TagastusAadress;

  or or_1 (or_1_out, mret, Katkestus);
  Multiplexer #(.width(32)) multiplexer_1 (
    .in0(adder_1_out), .in1(ALU_valjund), .out(TagastusAadress), .sel(instruction_decoder_1_pc_controll[0]));
  not not_1 (not_1_out, instruction_decoder_1_pc_controll[1]);
  Multiplexer #(.width(32)) multiplexer_2 (
    .in0(TagastusAadress), .in1(KatkestuseAadress), .out(multiplexer_2_out), .sel(or_1_out));
  Register #(.width(32)) PC (.D(multiplexer_2_out), .en(or_2_out), .clk(clk), .Q(juhise_aadress), .clr(reset));
  or or_2 (or_2_out, or_1_out, not_1_out);
  Multiplexer #(.width(32)) multiplexer_3 (
    .in0(32'h4), .in1(instruction_decoder_1_immidiate), .out(multiplexer_3_out), .sel(and_1_out));
  and and_1 (and_1_out, instruction_decoder_1_pc_controll[2], multiplexer_4_out);
  Adder #(.width(32)) adder_1 (.a(multiplexer_3_out), .b(juhise_aadress), .out(adder_1_out));  // open: cin, cout
  or or_3 (VJKA, juhise_aadress[0], juhise_aadress[1]);
  Multiplexer multiplexer_4 (
    .in0(or_4_out), .in1(not_2_out), .out(multiplexer_4_out), .sel(instruction_decoder_1_branch_select));
  not not_2 (not_2_out, or_4_out);
  S_R_Flip_Flop s_r_ff_1 (.R(and_11_out), .clk(clk), .Q(s_r_ff_1_q), .preset(Ext_Interrupt[0]));  // open: S, reset, Qn
  S_R_Flip_Flop s_r_ff_2 (.R(and_12_out), .clk(clk), .Q(s_r_ff_2_q), .preset(Ext_Interrupt[1]));  // open: S, reset, Qn
  or or_4 (or_4_out, ALU_valjund[31], ALU_valjund[30], ALU_valjund[29], ALU_valjund[28], ALU_valjund[27], ALU_valjund[26], ALU_valjund[25], ALU_valjund[24], ALU_valjund[23], ALU_valjund[22], ALU_valjund[21], ALU_valjund[20], ALU_valjund[19], ALU_valjund[18], ALU_valjund[17], ALU_valjund[16], ALU_valjund[14], ALU_valjund[13], ALU_valjund[12], ALU_valjund[11], ALU_valjund[10], ALU_valjund[9], ALU_valjund[8], ALU_valjund[7], ALU_valjund[6], ALU_valjund[5], ALU_valjund[4], ALU_valjund[3], ALU_valjund[2], ALU_valjund[1], ALU_valjund[0], ALU_valjund[15]);
  or or_5 (or_5_out, tundmatu_opcode, reset);
  or or_6 (or_6_out, or_5_out, and_2_out);
  or or_7 (or_7_out, or_6_out, and_3_out);
  or or_8 (or_8_out, or_7_out, and_4_out);
  or or_9 (or_9_out, or_8_out, and_5_out);
  or or_10 (or_10_out, or_9_out, and_6_out);
  or or_11 (or_11_out, or_10_out, and_7_out);
  or or_12 (or_12_out, or_11_out, and_8_out);
  or or_13 (or_13_out, or_12_out, and_9_out);
  or or_14 (or_14_out, or_13_out, and_10_out);
  or or_15 (or_15_out, or_14_out, and_11_out);
  or or_16 (or_16_out, or_15_out, and_12_out);
  or or_17 (or_17_out, or_16_out, and_13_out);
  or or_18 (or_18_out, or_17_out, and_14_out);
  or or_19 (or_19_out, or_18_out, and_15_out);
  or or_20 (or_20_out, or_19_out, and_16_out);
  or or_21 (or_21_out, or_20_out, and_17_out);
  or or_22 (or_22_out, or_21_out, and_18_out);
  or or_23 (or_23_out, or_22_out, and_19_out);
  or or_24 (or_24_out, or_23_out, and_20_out);
  or or_25 (or_25_out, or_24_out, and_21_out);
  or or_26 (or_26_out, or_25_out, and_22_out);
  or or_27 (or_27_out, or_26_out, and_23_out);
  or or_28 (or_28_out, or_27_out, and_24_out);
  or or_29 (or_29_out, or_28_out, and_25_out);
  or or_30 (or_30_out, or_29_out, and_26_out);
  or or_31 (or_31_out, or_30_out, and_27_out);
  or or_32 (or_32_out, or_31_out, and_28_out);
  or or_33 (or_33_out, or_32_out, and_29_out);
  or or_34 (or_34_out, or_33_out, and_30_out);
  and and_2 (and_2_out, ~or_5_out, VJKA);  // AND_Gate
  and and_3 (and_3_out, ~or_6_out, 1'b0);  // AND_Gate
  and and_4 (and_4_out, ~or_7_out, 1'b0);  // AND_Gate
  and and_5 (and_5_out, ~or_8_out, 1'b0);  // AND_Gate
  and and_6 (and_6_out, ~or_9_out, 1'b0);  // AND_Gate
  and and_7 (and_7_out, ~or_10_out, 1'b0);  // AND_Gate
  and and_8 (and_8_out, ~or_11_out, 1'b0);  // AND_Gate
  and and_9 (and_9_out, ~or_12_out, 1'b0);  // AND_Gate
  and and_10 (and_10_out, ~or_13_out, 1'b0);  // AND_Gate
  and and_11 (and_11_out, ~or_14_out, s_r_ff_1_q);  // AND_Gate
  and and_12 (and_12_out, ~or_15_out, s_r_ff_2_q);  // AND_Gate
  and and_13 (and_13_out, ~or_16_out, Ext_Interrupt[2]);  // AND_Gate
  and and_14 (and_14_out, ~or_17_out, Ext_Interrupt[3]);  // AND_Gate
  and and_15 (and_15_out, ~or_18_out, Ext_Interrupt[4]);  // AND_Gate
  and and_16 (and_16_out, ~or_19_out, Ext_Interrupt[5]);  // AND_Gate
  and and_17 (and_17_out, ~or_20_out, Ext_Interrupt[6]);  // AND_Gate
  and and_18 (and_18_out, ~or_21_out, Ext_Interrupt[7]);  // AND_Gate
  and and_19 (and_19_out, ~or_22_out, Ext_Interrupt[8]);  // AND_Gate
  and and_20 (and_20_out, ~or_23_out, Ext_Interrupt[9]);  // AND_Gate
  and and_21 (and_21_out, ~or_24_out, Ext_Interrupt[10]);  // AND_Gate
  and and_22 (and_22_out, ~or_25_out, Ext_Interrupt[11]);  // AND_Gate
  and and_23 (and_23_out, ~or_26_out, Ext_Interrupt[12]);  // AND_Gate
  and and_24 (and_24_out, ~or_27_out, Ext_Interrupt[13]);  // AND_Gate
  and and_25 (and_25_out, ~or_28_out, Ext_Interrupt[14]);  // AND_Gate
  and and_26 (and_26_out, ~or_29_out, Ext_Interrupt[15]);  // AND_Gate
  and and_27 (and_27_out, ~or_30_out, Ext_Interrupt[16]);  // AND_Gate
  and and_28 (and_28_out, ~or_31_out, Ext_Interrupt[17]);  // AND_Gate
  and and_29 (and_29_out, ~or_32_out, Ext_Interrupt[18]);  // AND_Gate
  and and_30 (and_30_out, ~or_33_out, Ext_Interrupt[19]);  // AND_Gate
  assign controlled_buffer_1_out = or_5_out ? {32{1'b0}} : 32'bz;  // Controlled_Buffer controlled_buffer_1
  assign controlled_buffer_1_out = and_2_out ? 32'h4 : 32'bz;  // Controlled_Buffer controlled_buffer_2
  assign controlled_buffer_1_out = and_3_out ? 32'h8 : 32'bz;  // Controlled_Buffer controlled_buffer_3
  assign controlled_buffer_1_out = and_4_out ? 32'hc : 32'bz;  // Controlled_Buffer controlled_buffer_4
  assign controlled_buffer_1_out = and_5_out ? 32'h10 : 32'bz;  // Controlled_Buffer controlled_buffer_5
  assign controlled_buffer_1_out = and_6_out ? 32'h14 : 32'bz;  // Controlled_Buffer controlled_buffer_6
  assign controlled_buffer_1_out = and_7_out ? 32'h18 : 32'bz;  // Controlled_Buffer controlled_buffer_7
  assign controlled_buffer_1_out = and_8_out ? 32'h1c : 32'bz;  // Controlled_Buffer controlled_buffer_8
  assign controlled_buffer_1_out = and_9_out ? 32'h20 : 32'bz;  // Controlled_Buffer controlled_buffer_9
  assign controlled_buffer_1_out = and_10_out ? 32'h24 : 32'bz;  // Controlled_Buffer controlled_buffer_10
  assign controlled_buffer_1_out = and_11_out ? 32'h28 : 32'bz;  // Controlled_Buffer controlled_buffer_11
  assign controlled_buffer_1_out = and_12_out ? 32'h2c : 32'bz;  // Controlled_Buffer controlled_buffer_12
  assign controlled_buffer_1_out = and_13_out ? 32'h30 : 32'bz;  // Controlled_Buffer controlled_buffer_13
  assign controlled_buffer_1_out = and_14_out ? 32'h34 : 32'bz;  // Controlled_Buffer controlled_buffer_14
  assign controlled_buffer_1_out = and_15_out ? 32'h38 : 32'bz;  // Controlled_Buffer controlled_buffer_15
  assign controlled_buffer_1_out = and_16_out ? 32'h3c : 32'bz;  // Controlled_Buffer controlled_buffer_16
  assign controlled_buffer_1_out = and_17_out ? 32'h40 : 32'bz;  // Controlled_Buffer controlled_buffer_17
  assign controlled_buffer_1_out = and_18_out ? 32'h44 : 32'bz;  // Controlled_Buffer controlled_buffer_18
  assign controlled_buffer_1_out = and_19_out ? 32'h48 : 32'bz;  // Controlled_Buffer controlled_buffer_19
  assign controlled_buffer_1_out = and_20_out ? 32'h4c : 32'bz;  // Controlled_Buffer controlled_buffer_20
  assign controlled_buffer_1_out = and_21_out ? 32'h50 : 32'bz;  // Controlled_Buffer controlled_buffer_21
  assign controlled_buffer_1_out = and_22_out ? 32'h54 : 32'bz;  // Controlled_Buffer controlled_buffer_22
  assign controlled_buffer_1_out = and_23_out ? 32'h58 : 32'bz;  // Controlled_Buffer controlled_buffer_23
  assign controlled_buffer_1_out = and_24_out ? 32'h5c : 32'bz;  // Controlled_Buffer controlled_buffer_24
  assign controlled_buffer_1_out = and_25_out ? 32'h60 : 32'bz;  // Controlled_Buffer controlled_buffer_25
  assign controlled_buffer_1_out = and_26_out ? 32'h64 : 32'bz;  // Controlled_Buffer controlled_buffer_26
  assign controlled_buffer_1_out = and_27_out ? 32'h68 : 32'bz;  // Controlled_Buffer controlled_buffer_27
  assign controlled_buffer_1_out = and_28_out ? 32'h6c : 32'bz;  // Controlled_Buffer controlled_buffer_28
  assign controlled_buffer_1_out = and_29_out ? 32'h70 : 32'bz;  // Controlled_Buffer controlled_buffer_29
  assign controlled_buffer_1_out = and_30_out ? 32'h74 : 32'bz;  // Controlled_Buffer controlled_buffer_30
  Instruction_decoder instruction_decoder_1 (
    .Juhis(juhis), .Immidiate(instruction_decoder_1_immidiate), .Command(instruction_decoder_1_command),
    .Register_mux(instruction_decoder_1_register_mux), .ALU_src_A(instruction_decoder_1_alu_src_a),
    .rs1(instruction_decoder_1_rs1), .rs2(instruction_decoder_1_rs2), .rd(instruction_decoder_1_rd),
    .Data_type(instruction_decoder_1_data_type), .ALU_src_B(instruction_decoder_1_alu_src_b),
    .Write_enable(kirjuta_mallu), .CSR_write_enable(kirjutaCSR), .CSR_address(CSRaadress), .mret(mret),
    .Branch_select(instruction_decoder_1_branch_select), .PC_controll(instruction_decoder_1_pc_controll),
    .kehtiv_opcode(instruction_decoder_1_kehtiv_opcode));
  or or_35 (Katkestus, or_5_out, and_31_out);
  and and_31 (and_31_out, or_36_out, MIE);
  or or_36 (or_36_out, and_2_out, or_37_out);
  or or_37 (or_37_out, and_3_out, or_38_out);
  or or_38 (or_38_out, and_4_out, or_39_out);
  or or_39 (or_39_out, and_5_out, or_40_out);
  or or_40 (or_40_out, and_6_out, or_41_out);
  or or_41 (or_41_out, and_7_out, or_42_out);
  or or_42 (or_42_out, and_8_out, or_43_out);
  or or_43 (or_43_out, and_9_out, or_44_out);
  or or_44 (or_44_out, and_10_out, or_45_out);
  or or_45 (or_45_out, and_11_out, or_46_out);
  or or_46 (or_46_out, and_12_out, or_47_out);
  or or_47 (or_47_out, and_13_out, or_48_out);
  or or_48 (or_48_out, and_14_out, or_49_out);
  or or_49 (or_49_out, and_15_out, or_50_out);
  or or_50 (or_50_out, and_16_out, or_51_out);
  or or_51 (or_51_out, and_17_out, or_52_out);
  or or_52 (or_52_out, and_18_out, or_53_out);
  or or_53 (or_53_out, and_19_out, or_54_out);
  or or_54 (or_54_out, and_20_out, or_55_out);
  or or_55 (or_55_out, and_21_out, or_56_out);
  or or_56 (or_56_out, and_22_out, or_57_out);
  or or_57 (or_57_out, and_23_out, or_58_out);
  or or_58 (or_58_out, and_24_out, or_59_out);
  or or_59 (or_59_out, and_25_out, or_60_out);
  or or_60 (or_60_out, and_26_out, or_61_out);
  or or_61 (or_61_out, and_27_out, or_62_out);
  or or_62 (or_62_out, and_28_out, or_63_out);
  or or_63 (or_63_out, and_29_out, or_64_out);
  or or_64 (or_64_out, and_30_out, or_34_out);
  not not_3 (tundmatu_opcode, instruction_decoder_1_kehtiv_opcode);
  assign KatkestuseAadress = Katkestus ? controlled_buffer_1_out : 32'bz;  // Controlled_Buffer controlled_buffer_31
  and and_32 (and_32_out, ~undriven_2, undriven);  // AND_Gate
  or or_65 (or_65_out, undriven_2, and_32_out);
  assign controlled_buffer_32_out = and_32_out ? 32'h20 : 32'bz;  // Controlled_Buffer controlled_buffer_32
  // OR_Gate or_66 has open pins: in0=and_32_out, in1=undriven_3, out=open
  Registers registers_1 (
    .Read_address_2(instruction_decoder_1_rs2), .Read_address_1(instruction_decoder_1_rs1),
    .Data_in(multiplexer_11_out), .Write_address(instruction_decoder_1_rd), .Clock(clk),
    .Register_output_2(registers_1_register_output_2), .Register_output_1(registers_1_register_output_1));  // open: Reset
  Multiplexer #(.width(32)) multiplexer_5 (
    .in0(juhise_aadress), .in1(registers_1_register_output_1), .out(multiplexer_5_out),
    .sel(instruction_decoder_1_alu_src_a));
  Multiplexer #(.width(32)) multiplexer_6 (
    .in0(registers_1_register_output_2), .in1(instruction_decoder_1_immidiate), .out(multiplexer_6_out),
    .sel(instruction_decoder_1_alu_src_b));
  ALU alu_1 (
    .Juhend(instruction_decoder_1_command), .a1(multiplexer_5_out), .a2(multiplexer_6_out),
    .Tulemus(ALU_valjund));
  Comparator #(.mode("unsigned"), .width(12)) comparator_1 (
    .a(CSRaadress), .b(12'h301), .eq(comparator_1_eq));  // open: gt, lt
  Comparator #(.mode("unsigned"), .width(12)) comparator_2 (
    .a(CSRaadress), .b({12{1'b0}}), .eq(comparator_2_eq));  // open: gt, lt
  Comparator #(.mode("unsigned"), .width(12)) comparator_3 (
    .a(CSRaadress), .b(12'hf12), .eq(comparator_3_eq));  // open: gt, lt
  Comparator #(.mode("unsigned"), .width(12)) comparator_4 (
    .a(CSRaadress), .b(12'hf13), .eq(comparator_4_eq));  // open: gt, lt
  Comparator #(.mode("unsigned"), .width(12)) comparator_5 (
    .a(CSRaadress), .b(12'hf14), .eq(comparator_5_eq));  // open: gt, lt
  Comparator #(.mode("unsigned"), .width(12)) comparator_6 (
    .a(CSRaadress), .b(12'h341), .eq(comparator_6_eq));  // open: gt, lt
  Comparator #(.mode("unsigned"), .width(12)) comparator_7 (
    .a(CSRaadress), .b(12'hb00), .eq(comparator_7_eq));  // open: gt, lt
  Comparator #(.mode("unsigned"), .width(12)) comparator_8 (
    .a(CSRaadress), .b(12'h300), .eq(comparator_8_eq));  // open: gt, lt
  and and_33 (and_33_out, comparator_6_eq, kirjutaCSR);
  and and_34 (and_34_out, comparator_8_eq, kirjutaCSR);
  Multiplexer #(.select(3), .width(32)) multiplexer_7 (
    .in5(registers_1_register_output_2), .in6({{16{1'b0}}, registers_1_register_output_2[15:0]}),
    .in7({{24{1'b0}}, registers_1_register_output_2[7:0]}), .out(multiplexer_7_out),
    .sel(instruction_decoder_1_data_type));  // open: in0, in1, in2, in3, in4
  Multiplexer #(.select(3), .width(4)) multiplexer_8 (
    .in5(4'b1111), .in6(4'b0011), .in7(4'b0001), .out(multiplexer_8_out),
    .sel(instruction_decoder_1_data_type));  // open: in0, in1, in2, in3, in4
  Multiplexer #(.width(32)) multiplexer_9 (
    .in0(ALU_valjund), .in1(TagastusAadress), .out(multiplexer_9_out), .sel(Katkestus));
  Multiplexer #(.width(32)) multiplexer_10 (
    .in0(ALU_valjund), .in1({register_2_q[29:16], 1'b0, register_2_q[15:3], 1'b0, register_2_q[2:0]}),
    .out(multiplexer_10_out), .sel(reset));
  Shifter #(.width(4)) shifter_1 (.in(multiplexer_8_out), .\dist (ALU_valjund[1:0]), .out(shifter_1_out));
  Register #(.width(30)) register_1 (
    .D(multiplexer_9_out[31:2]), .en(or_67_out), .clk(clk), .Q(register_1_q));  // open: clr
  or or_67 (or_67_out, Katkestus, and_33_out);
  Register #(.width(32)) register_2 (
    .D(multiplexer_10_out), .en(or_68_out), .clk(clk),
    .Q({register_2_q[29:16], register_2_q_2[17], register_2_q[15:3], MIE, register_2_q[2:0]}));  // open: clr
  or or_68 (or_68_out, reset, and_34_out);
  // Probe on ALU_valjund
  Shifter #(.width(32)) shifter_2 (.in(multiplexer_7_out), .\dist ({ALU_valjund[1:0], 3'b000}), .out(shifter_2_out));
  assign not_4_out = ~{{8{shifter_1_out[3]}}, {8{shifter_1_out[2]}}, {8{shifter_1_out[1]}}, {8{shifter_1_out[0]}}};  // NOT_Gate not_4, 32 bits wide
  assign and_35_out = malu_sisend & not_4_out;  // AND_Gate and_35, 32 bits wide
  Counter #(.max('hffffffff), .width(32)) counter_1 (
    .count(1'b1), .Q(counter_1_q), .up(1'b1), .clk(clk));  // open: load, D, carry, clr
  assign or_69_out = shifter_2_out | and_35_out;  // OR_Gate or_69, 32 bits wide
  assign malu_valjund = kirjuta_mallu ? or_69_out : 32'bz;  // Controlled_Buffer controlled_buffer_33
  assign CSRvaljund = comparator_1_eq ? 32'h80000100 : 32'bz;  // Controlled_Buffer controlled_buffer_34
  assign CSRvaljund = comparator_2_eq ? {32{1'b0}} : 32'bz;  // Controlled_Buffer controlled_buffer_35
  assign CSRvaljund = comparator_3_eq ? {32{1'b0}} : 32'bz;  // Controlled_Buffer controlled_buffer_36
  assign CSRvaljund = comparator_4_eq ? {32{1'b0}} : 32'bz;  // Controlled_Buffer controlled_buffer_37
  assign CSRvaljund = comparator_5_eq ? {32{1'b0}} : 32'bz;  // Controlled_Buffer controlled_buffer_38
  assign CSRvaljund = comparator_6_eq ? {register_1_q, 2'b00} : 32'bz;  // Controlled_Buffer controlled_buffer_39
  assign KatkestuseAadress = mret ? {register_1_q, 2'b00} : 32'bz;  // Controlled_Buffer controlled_buffer_40
  assign CSRvaljund = comparator_7_eq ? counter_1_q : 32'bz;  // Controlled_Buffer controlled_buffer_41
  assign CSRvaljund = comparator_8_eq ? {register_2_q[29:16], register_2_q_2[17], register_2_q[15:3], MIE, register_2_q[2:0]} : 32'bz;  // Controlled_Buffer controlled_buffer_42
  assign not_5_out = ~ALU_valjund[1:0];  // NOT_Gate not_5, 2 bits wide
  Shifter #(.shift("lr"), .width(32)) shifter_3 (.in(malu_sisend), .\dist ({not_5_out, 3'b000}), .out(shifter_3_out));
  assign bit_extender_1_out = {{16{shifter_3_out[15]}}, shifter_3_out[15:0]};  // Bit_Extender bit_extender_1
  assign bit_extender_2_out = {{16{1'b0}}, shifter_3_out[15:0]};  // Bit_Extender bit_extender_2
  assign bit_extender_3_out = {{24{shifter_3_out[7]}}, shifter_3_out[7:0]};  // Bit_Extender bit_extender_3
  assign bit_extender_4_out = {{24{1'b0}}, shifter_3_out[7:0]};  // Bit_Extender bit_extender_4
  Multiplexer #(.select(2), .width(32)) multiplexer_11 (
    .in0(adder_1_out), .in1(CSRvaljund), .in2(ALU_valjund), .in3(multiplexer_12_out),
    .out(multiplexer_11_out), .sel(instruction_decoder_1_register_mux));
  Multiplexer #(.select(3), .width(32)) multiplexer_12 (
    .in0(shifter_3_out), .in1(bit_extender_1_out), .in2(bit_extender_2_out), .in3(bit_extender_3_out),
    .in4(bit_extender_4_out), .out(multiplexer_12_out), .sel(instruction_decoder_1_data_type));  // open: in5, in6, in7

  // Other names for the same wires on the sheet: ALUvaljund[31:0] = ALU_valjund

  // Notes on the sheet:
  //   malu_valjund: pull=down
endmodule

module ALU (
  input  [4:0] Juhend,
  input  [31:0] a1,
  input  [31:0] a2,
  output [31:0] Tulemus
);

  wire adder_1_cout, comparator_1_lt, decoder_1_out1, decoder_1_out2, not_1_out, or_1_out;
  wire [31:0] adder_1_out, and_1_out, bit_extender_1_out, bit_extender_2_out, bit_extender_3_out,
       divider_1_out, divider_1_rem, divider_2_out, divider_2_rem, multiplier_1_cout, multiplier_1_out,
       multiplier_2_cout, multiplier_2_out, or_2_out, shifter_1_out, shifter_2_out, shifter_3_out, xor_1_out,
       xor_2_out;

  Decoder #(.enable("false"), .select(5)) decoder_1 (
    .out1(decoder_1_out1), .out2(decoder_1_out2), .sel(Juhend));  // open: out0, out3, out4, out5, out6, out7, out8, out9, out10, out11, out12, out13, out14, out15, out16, out17, out18, out19, out20, out21, out22, out23, out24, out25, out26, out27, out28, out29, out30, out31
  or or_1 (or_1_out, decoder_1_out1, decoder_1_out2);
  assign bit_extender_1_out = {{31{or_1_out}}, or_1_out};  // Bit_Extender bit_extender_1
  assign xor_1_out = bit_extender_1_out ^ a2;  // XOR_Gate xor_1, 32 bits wide
  Adder #(.width(32)) adder_1 (.a(a1), .b(xor_1_out), .out(adder_1_out), .cin(or_1_out), .cout(adder_1_cout));
  not not_1 (not_1_out, adder_1_cout);
  Shifter #(.width(32)) shifter_1 (.in(a1), .\dist (a2[4:0]), .out(shifter_1_out));
  Shifter #(.shift("lr"), .width(32)) shifter_2 (.in(a1), .\dist (a2[4:0]), .out(shifter_2_out));
  Shifter #(.shift("ar"), .width(32)) shifter_3 (.in(a1), .\dist (a2[4:0]), .out(shifter_3_out));
  assign and_1_out = a1 & a2;  // AND_Gate and_1, 32 bits wide
  assign or_2_out = a1 | a2;  // OR_Gate or_2, 32 bits wide
  assign xor_2_out = a1 ^ a2;  // XOR_Gate xor_2, 32 bits wide
  Multiplier #(.mode("twosComplement"), .width(32)) multiplier_1 (
    .a(a1), .b(a2), .out(multiplier_1_out), .cout(multiplier_1_cout));  // open: cin
  Multiplier #(.width(32)) multiplier_2 (
    .a(a1), .b(a2), .out(multiplier_2_out), .cout(multiplier_2_cout));  // open: cin
  Divider #(.mode("twosComplement"), .width(32)) divider_1 (
    .a(a1), .b(a2), .out(divider_1_out), .rem(divider_1_rem));  // open: upper
  Divider #(.width(32)) divider_2 (.a(a1), .b(a2), .out(divider_2_out), .rem(divider_2_rem));  // open: upper
  Comparator #(.width(32)) comparator_1 (.a(a1), .b(a2), .lt(comparator_1_lt));  // open: gt, eq
  assign bit_extender_2_out = {{31{1'b0}}, not_1_out};  // Bit_Extender bit_extender_2
  assign bit_extender_3_out = {{31{1'b0}}, comparator_1_lt};  // Bit_Extender bit_extender_3
  Multiplexer #(.select(5), .width(32)) multiplexer_1 (
    .in0(adder_1_out), .in1(adder_1_out), .in2(bit_extender_2_out), .in3(shifter_1_out), .in4(shifter_2_out),
    .in5(shifter_3_out), .in6(and_1_out), .in7(or_2_out), .in8(xor_2_out), .in9(multiplier_1_out),
    .in10(multiplier_1_cout), .in11(multiplier_2_out), .in12(multiplier_2_cout), .in13(divider_1_out),
    .in14(divider_1_rem), .in15(divider_2_out), .in16(divider_2_rem), .in17(bit_extender_3_out),
    .out(Tulemus), .sel(Juhend));  // open: in18, in19, in20, in21, in22, in23, in24, in25, in26, in27, in28, in29, in30, in31

  // Notes on the sheet:
  //   Liida/Lahuta
  //   Add/Subtract
  //   Loogiline vasaknihutus
  //   Logical shift left
  //   Loogiline paremnihutus
  //   Logical shift right
  //   Aritmeetiline paremnihutus
  //   Arithmetic right shift
  //   AND värav
  //   AND gate
  //   OR värav
  //   OR gate
  //   XOR värav
  //   XOR gate
  //   Märgiga korrutus
  //   Signed multiplication
  //   Märgita korrutus
  //   Unsigned multiplication
  //   Märgiga Jagamine
  //   Signed division
  //   Märgita jagamine
  //   Unsigned division
  //   Märgiga võrdlus
  //   Signed comparison
endmodule

module Registers (
  input  [4:0] Read_address_1,
  input  [31:0] Data_in,
  input  Reset,
  input  Clock,
  input  [4:0] Read_address_2,
  input  [4:0] Write_address,
  output [31:0] Register_output_1,
  output [31:0] Register_output_2
);

  wire decoder_1_out1, decoder_1_out2, decoder_1_out3, decoder_1_out4, decoder_1_out5, decoder_1_out6,
       decoder_1_out7, decoder_1_out8, decoder_1_out9, decoder_1_out10, decoder_1_out11, decoder_1_out12,
       decoder_1_out13, decoder_1_out14, decoder_1_out15, decoder_1_out16, decoder_1_out17, decoder_1_out18,
       decoder_1_out19, decoder_1_out20, decoder_1_out21, decoder_1_out22, decoder_1_out23, decoder_1_out24,
       decoder_1_out25, decoder_1_out26, decoder_1_out27, decoder_1_out28, decoder_1_out29, decoder_1_out30,
       decoder_1_out31;
  wire [31:0] X1_q, X2_q, X3_q, X4_q, X5_q, X6_q, X7_q, X8_q, X9_q, X10_q, X11_q, X12_q, X13_q, X14_q, X15_q,
       X16_q, X17_q, X18_q, X19_q, X20_q, X21_q, X22_q, X23_q, X24_q, X25_q, X26_q, X27_q, X28_q, X29_q,
       X30_q, X31_q;

  Decoder #(.enable("false"), .select(5)) decoder_1 (
    .out1(decoder_1_out1), .out2(decoder_1_out2), .out3(decoder_1_out3), .out4(decoder_1_out4),
    .out5(decoder_1_out5), .out6(decoder_1_out6), .out7(decoder_1_out7), .out8(decoder_1_out8),
    .out9(decoder_1_out9), .out10(decoder_1_out10), .out11(decoder_1_out11), .out12(decoder_1_out12),
    .out13(decoder_1_out13), .out14(decoder_1_out14), .out15(decoder_1_out15), .out16(decoder_1_out16),
    .out17(decoder_1_out17), .out18(decoder_1_out18), .out19(decoder_1_out19), .out20(decoder_1_out20),
    .out21(decoder_1_out21), .out22(decoder_1_out22), .out23(decoder_1_out23), .out24(decoder_1_out24),
    .out25(decoder_1_out25), .out26(decoder_1_out26), .out27(decoder_1_out27), .out28(decoder_1_out28),
    .out29(decoder_1_out29), .out30(decoder_1_out30), .out31(decoder_1_out31), .sel(Write_address));  // open: out0
  Register #(.width(32)) X28 (.D(Data_in), .en(decoder_1_out28), .clk(Clock), .Q(X28_q), .clr(Reset));
  Register #(.width(32)) X29 (.D(Data_in), .en(decoder_1_out29), .clk(Clock), .Q(X29_q), .clr(Reset));
  Register #(.width(32)) X30 (.D(Data_in), .en(decoder_1_out30), .clk(Clock), .Q(X30_q), .clr(Reset));
  Register #(.width(32)) X31 (.D(Data_in), .en(decoder_1_out31), .clk(Clock), .Q(X31_q), .clr(Reset));
  Register #(.width(32)) X24 (.D(Data_in), .en(decoder_1_out24), .clk(Clock), .Q(X24_q), .clr(Reset));
  Register #(.width(32)) X25 (.D(Data_in), .en(decoder_1_out25), .clk(Clock), .Q(X25_q), .clr(Reset));
  Register #(.width(32)) X26 (.D(Data_in), .en(decoder_1_out26), .clk(Clock), .Q(X26_q), .clr(Reset));
  Register #(.width(32)) X27 (.D(Data_in), .en(decoder_1_out27), .clk(Clock), .Q(X27_q), .clr(Reset));
  Register #(.width(32)) X20 (.D(Data_in), .en(decoder_1_out20), .clk(Clock), .Q(X20_q), .clr(Reset));
  Register #(.width(32)) X21 (.D(Data_in), .en(decoder_1_out21), .clk(Clock), .Q(X21_q), .clr(Reset));
  Register #(.width(32)) X22 (.D(Data_in), .en(decoder_1_out22), .clk(Clock), .Q(X22_q), .clr(Reset));
  Register #(.width(32)) X23 (.D(Data_in), .en(decoder_1_out23), .clk(Clock), .Q(X23_q), .clr(Reset));
  Register #(.width(32)) X16 (.D(Data_in), .en(decoder_1_out16), .clk(Clock), .Q(X16_q), .clr(Reset));
  Register #(.width(32)) X17 (.D(Data_in), .en(decoder_1_out17), .clk(Clock), .Q(X17_q), .clr(Reset));
  Register #(.width(32)) X18 (.D(Data_in), .en(decoder_1_out18), .clk(Clock), .Q(X18_q), .clr(Reset));
  Register #(.width(32)) X19 (.D(Data_in), .en(decoder_1_out19), .clk(Clock), .Q(X19_q), .clr(Reset));
  Register #(.width(32)) X12 (.D(Data_in), .en(decoder_1_out12), .clk(Clock), .Q(X12_q), .clr(Reset));
  Register #(.width(32)) X13 (.D(Data_in), .en(decoder_1_out13), .clk(Clock), .Q(X13_q), .clr(Reset));
  Register #(.width(32)) X14 (.D(Data_in), .en(decoder_1_out14), .clk(Clock), .Q(X14_q), .clr(Reset));
  Register #(.width(32)) X15 (.D(Data_in), .en(decoder_1_out15), .clk(Clock), .Q(X15_q), .clr(Reset));
  Register #(.width(32)) X8 (.D(Data_in), .en(decoder_1_out8), .clk(Clock), .Q(X8_q), .clr(Reset));
  Register #(.width(32)) X9 (.D(Data_in), .en(decoder_1_out9), .clk(Clock), .Q(X9_q), .clr(Reset));
  Register #(.width(32)) X10 (.D(Data_in), .en(decoder_1_out10), .clk(Clock), .Q(X10_q), .clr(Reset));
  Register #(.width(32)) X11 (.D(Data_in), .en(decoder_1_out11), .clk(Clock), .Q(X11_q), .clr(Reset));
  Register #(.width(32)) X4 (.D(Data_in), .en(decoder_1_out4), .clk(Clock), .Q(X4_q), .clr(Reset));
  Register #(.width(32)) X5 (.D(Data_in), .en(decoder_1_out5), .clk(Clock), .Q(X5_q), .clr(Reset));
  Register #(.width(32)) X6 (.D(Data_in), .en(decoder_1_out6), .clk(Clock), .Q(X6_q), .clr(Reset));
  Register #(.width(32)) X7 (.D(Data_in), .en(decoder_1_out7), .clk(Clock), .Q(X7_q), .clr(Reset));
  Register #(.width(32)) X1 (.D(Data_in), .en(decoder_1_out1), .clk(Clock), .Q(X1_q), .clr(Reset));
  Register #(.width(32)) X2 (.D(Data_in), .en(decoder_1_out2), .clk(Clock), .Q(X2_q), .clr(Reset));
  Register #(.width(32)) X3 (.D(Data_in), .en(decoder_1_out3), .clk(Clock), .Q(X3_q), .clr(Reset));
  Multiplexer #(.select(5), .width(32)) multiplexer_1 (
    .in0({32{1'b0}}), .in1(X1_q), .in2(X2_q), .in3(X3_q), .in4(X4_q), .in5(X5_q), .in6(X6_q), .in7(X7_q),
    .in8(X8_q), .in9(X9_q), .in10(X10_q), .in11(X11_q), .in12(X12_q), .in13(X13_q), .in14(X14_q),
    .in15(X15_q), .in16(X16_q), .in17(X17_q), .in18(X18_q), .in19(X19_q), .in20(X20_q), .in21(X21_q),
    .in22(X22_q), .in23(X23_q), .in24(X24_q), .in25(X25_q), .in26(X26_q), .in27(X27_q), .in28(X28_q),
    .in29(X29_q), .in30(X30_q), .in31(X31_q), .out(Register_output_1), .sel(Read_address_1));
  Multiplexer #(.select(5), .width(32)) multiplexer_2 (
    .in0({32{1'b0}}), .in1(X1_q), .in2(X2_q), .in3(X3_q), .in4(X4_q), .in5(X5_q), .in6(X6_q), .in7(X7_q),
    .in8(X8_q), .in9(X9_q), .in10(X10_q), .in11(X11_q), .in12(X12_q), .in13(X13_q), .in14(X14_q),
    .in15(X15_q), .in16(X16_q), .in17(X17_q), .in18(X18_q), .in19(X19_q), .in20(X20_q), .in21(X21_q),
    .in22(X22_q), .in23(X23_q), .in24(X24_q), .in25(X25_q), .in26(X26_q), .in27(X27_q), .in28(X28_q),
    .in29(X29_q), .in30(X30_q), .in31(X31_q), .out(Register_output_2), .sel(Read_address_2));

  // Notes on the sheet:
  //   X0
endmodule

module Instruction_decoder (
  input  [31:0] Juhis,
  output [31:0] Immidiate,
  output [4:0] Command,
  output [1:0] Register_mux,
  output ALU_src_A,
  output [4:0] rs1,
  output [4:0] rs2,
  output [4:0] rd,
  output [2:0] Data_type,
  output ALU_src_B,
  output Write_enable,
  output CSR_write_enable,
  output [11:0] CSR_address,
  output mret,
  output Branch_select,
  output [2:0] PC_controll,
  output kehtiv_opcode
);

  wire and_1_out, and_2_out, and_3_out, and_4_out, and_5_out, and_6_out, and_7_out, and_8_out, and_9_out,
       and_10_out, and_11_out, and_12_out, and_13_out, and_14_out, and_15_out, and_16_out, and_17_out,
       and_18_out, and_19_out, and_20_out, and_21_out, and_22_out, and_23_out, and_24_out, and_25_out,
       and_26_out, and_27_out, and_28_out, and_29_out, and_30_out, and_31_out, and_32_out, and_33_out,
       and_34_out, and_35_out, and_36_out, and_37_out, and_38_out, and_39_out, and_40_out, and_41_out,
       and_42_out, and_43_out, and_44_out, and_45_out, and_46_out, and_47_out, and_48_out, and_49_out,
       and_50_out, and_51_out, and_52_out, and_53_out, and_54_out, and_55_out, and_56_out, or_1_out;
  wire [11:0] bit_extender_3_out;
  wire [31:0] bit_extender_1_out, bit_extender_2_out, bit_extender_4_out, bit_extender_5_out,
       bit_extender_6_out, bit_extender_7_out;

  and and_1 (and_1_out, Juhis[0], Juhis[1], ~Juhis[2], ~Juhis[3], Juhis[4], Juhis[5], ~Juhis[6]);  // AND_Gate
  and and_2 (and_2_out, Juhis[0], Juhis[1], ~Juhis[2], ~Juhis[3], Juhis[4], Juhis[5], ~Juhis[6], ~Juhis[12], ~Juhis[13], ~Juhis[14], ~Juhis[25], ~Juhis[26], ~Juhis[27], ~Juhis[28], ~Juhis[29], ~Juhis[30], ~Juhis[31]);  // AND_Gate
  and and_3 (and_3_out, Juhis[0], Juhis[1], ~Juhis[2], ~Juhis[3], Juhis[4], Juhis[5], ~Juhis[6], ~Juhis[12], ~Juhis[13], ~Juhis[14], ~Juhis[25], ~Juhis[26], ~Juhis[27], ~Juhis[28], ~Juhis[29], Juhis[30], ~Juhis[31]);  // AND_Gate
  and and_4 (and_4_out, Juhis[0], Juhis[1], ~Juhis[2], ~Juhis[3], Juhis[4], Juhis[5], ~Juhis[6], Juhis[12], Juhis[13], Juhis[14], ~Juhis[25], ~Juhis[26], ~Juhis[27], ~Juhis[28], ~Juhis[29], ~Juhis[30], ~Juhis[31]);  // AND_Gate
  and and_5 (and_5_out, Juhis[0], Juhis[1], ~Juhis[2], ~Juhis[3], Juhis[4], Juhis[5], ~Juhis[6], ~Juhis[12], Juhis[13], Juhis[14], ~Juhis[25], ~Juhis[26], ~Juhis[27], ~Juhis[28], ~Juhis[29], ~Juhis[30], ~Juhis[31]);  // AND_Gate
  and and_6 (and_6_out, Juhis[0], Juhis[1], ~Juhis[2], ~Juhis[3], Juhis[4], Juhis[5], ~Juhis[6], ~Juhis[12], ~Juhis[13], Juhis[14], ~Juhis[25], ~Juhis[26], ~Juhis[27], ~Juhis[28], ~Juhis[29], ~Juhis[30], ~Juhis[31]);  // AND_Gate
  and and_7 (and_7_out, Juhis[0], Juhis[1], ~Juhis[2], ~Juhis[3], Juhis[4], Juhis[5], ~Juhis[6], Juhis[12], ~Juhis[13], ~Juhis[14], ~Juhis[25], ~Juhis[26], ~Juhis[27], ~Juhis[28], ~Juhis[29], ~Juhis[30], ~Juhis[31]);  // AND_Gate
  and and_8 (and_8_out, Juhis[0], Juhis[1], ~Juhis[2], ~Juhis[3], Juhis[4], Juhis[5], ~Juhis[6], ~Juhis[12], Juhis[13], ~Juhis[14], ~Juhis[25], ~Juhis[26], ~Juhis[27], ~Juhis[28], ~Juhis[29], ~Juhis[30], ~Juhis[31]);  // AND_Gate
  and and_9 (and_9_out, Juhis[0], Juhis[1], ~Juhis[2], ~Juhis[3], Juhis[4], Juhis[5], ~Juhis[6], Juhis[12], Juhis[13], ~Juhis[14], ~Juhis[25], ~Juhis[26], ~Juhis[27], ~Juhis[28], ~Juhis[29], ~Juhis[30], ~Juhis[31]);  // AND_Gate
  and and_10 (and_10_out, Juhis[0], Juhis[1], ~Juhis[2], ~Juhis[3], Juhis[4], Juhis[5], ~Juhis[6], Juhis[12], Juhis[13], ~Juhis[14], ~Juhis[25], ~Juhis[26], ~Juhis[27], ~Juhis[28], ~Juhis[29], ~Juhis[30], ~Juhis[31]);  // AND_Gate
  and and_11 (and_11_out, Juhis[0], Juhis[1], ~Juhis[2], ~Juhis[3], Juhis[4], Juhis[5], ~Juhis[6], Juhis[12], Juhis[13], ~Juhis[14], ~Juhis[25], ~Juhis[26], ~Juhis[27], ~Juhis[28], ~Juhis[29], Juhis[30], ~Juhis[31]);  // AND_Gate
  assign rd = and_1_out ? Juhis[11:7] : 5'bz;  // Controlled_Buffer controlled_buffer_1
  assign rs1 = and_1_out ? Juhis[19:15] : 5'bz;  // Controlled_Buffer controlled_buffer_2
  assign rs2 = and_1_out ? Juhis[24:20] : 5'bz;  // Controlled_Buffer controlled_buffer_3
  assign ALU_src_B = and_1_out ? 1'b0 : 1'bz;  // Controlled_Buffer controlled_buffer_4
  assign Write_enable = and_1_out ? 1'b0 : 1'bz;  // Controlled_Buffer controlled_buffer_5
  assign ALU_src_A = and_1_out ? 1'b1 : 1'bz;  // Controlled_Buffer controlled_buffer_6
  assign Data_type = and_1_out ? 3'b000 : 3'bz;  // Controlled_Buffer controlled_buffer_7
  assign Register_mux = and_1_out ? 2'b10 : 2'bz;  // Controlled_Buffer controlled_buffer_8
  assign CSR_write_enable = and_1_out ? 1'b0 : 1'bz;  // Controlled_Buffer controlled_buffer_9
  assign CSR_address = and_1_out ? {12{1'b0}} : 12'bz;  // Controlled_Buffer controlled_buffer_10
  assign PC_controll = and_1_out ? 3'b000 : 3'bz;  // Controlled_Buffer controlled_buffer_11
  assign mret = and_1_out ? 1'b0 : 1'bz;  // Controlled_Buffer controlled_buffer_12
  assign kehtiv_opcode = and_1_out ? 1'b1 : 1'bz;  // Controlled_Buffer controlled_buffer_13
  assign Command = and_2_out ? {5{1'b0}} : 5'bz;  // Controlled_Buffer controlled_buffer_14
  assign Command = and_3_out ? 5'b00001 : 5'bz;  // Controlled_Buffer controlled_buffer_15
  assign Command = and_4_out ? 5'b00110 : 5'bz;  // Controlled_Buffer controlled_buffer_16
  assign Command = and_5_out ? 5'b00111 : 5'bz;  // Controlled_Buffer controlled_buffer_17
  assign Command = and_6_out ? 5'b01000 : 5'bz;  // Controlled_Buffer controlled_buffer_18
  assign Command = and_7_out ? 5'b00011 : 5'bz;  // Controlled_Buffer controlled_buffer_19
  assign Command = and_8_out ? 5'b10001 : 5'bz;  // Controlled_Buffer controlled_buffer_20
  assign Command = and_9_out ? 5'b00010 : 5'bz;  // Controlled_Buffer controlled_buffer_21
  assign Command = and_10_out ? 5'b00100 : 5'bz;  // Controlled_Buffer controlled_buffer_22
  assign Command = and_11_out ? 5'b00101 : 5'bz;  // Controlled_Buffer controlled_buffer_23
  and and_12 (and_12_out, Juhis[0], Juhis[1], Juhis[2], ~Juhis[3], Juhis[4], Juhis[5], ~Juhis[6]);  // AND_Gate
  and and_13 (and_13_out, Juhis[0], Juhis[1], Juhis[2], ~Juhis[3], Juhis[4], ~Juhis[5], ~Juhis[6]);  // AND_Gate
  assign rd = and_12_out ? Juhis[11:7] : 5'bz;  // Controlled_Buffer controlled_buffer_24
  assign Immidiate = and_12_out ? {Juhis[31:12], {12{1'b0}}} : 32'bz;  // Controlled_Buffer controlled_buffer_25
  assign rs1 = and_12_out ? {5{1'b0}} : 5'bz;  // Controlled_Buffer controlled_buffer_26
  assign rd = and_13_out ? Juhis[11:7] : 5'bz;  // Controlled_Buffer controlled_buffer_27
  assign Immidiate = and_13_out ? {Juhis[31:12], {12{1'b0}}} : 32'bz;  // Controlled_Buffer controlled_buffer_28
  assign rs1 = and_13_out ? {5{1'b0}} : 5'bz;  // Controlled_Buffer controlled_buffer_29
  assign rs2 = and_12_out ? {5{1'b0}} : 5'bz;  // Controlled_Buffer controlled_buffer_30
  assign Command = and_12_out ? 5'b00111 : 5'bz;  // Controlled_Buffer controlled_buffer_31
  assign Register_mux = and_12_out ? 2'b10 : 2'bz;  // Controlled_Buffer controlled_buffer_32
  assign ALU_src_B = and_12_out ? 1'b1 : 1'bz;  // Controlled_Buffer controlled_buffer_33
  assign CSR_write_enable = and_12_out ? 1'b0 : 1'bz;  // Controlled_Buffer controlled_buffer_34
  assign CSR_address = and_12_out ? {12{1'b0}} : 12'bz;  // Controlled_Buffer controlled_buffer_35
  assign PC_controll = and_12_out ? 3'b000 : 3'bz;  // Controlled_Buffer controlled_buffer_36
  assign mret = and_12_out ? 1'b0 : 1'bz;  // Controlled_Buffer controlled_buffer_37
  assign kehtiv_opcode = and_12_out ? 1'b1 : 1'bz;  // Controlled_Buffer controlled_buffer_38
  assign rs2 = and_13_out ? {5{1'b0}} : 5'bz;  // Controlled_Buffer controlled_buffer_39
  assign Command = and_13_out ? 5'b00111 : 5'bz;  // Controlled_Buffer controlled_buffer_40
  assign Register_mux = and_13_out ? 2'b10 : 2'bz;  // Controlled_Buffer controlled_buffer_41
  assign ALU_src_B = and_13_out ? 1'b1 : 1'bz;  // Controlled_Buffer controlled_buffer_42
  assign CSR_write_enable = and_13_out ? 1'b0 : 1'bz;  // Controlled_Buffer controlled_buffer_43
  assign CSR_address = and_13_out ? {12{1'b0}} : 12'bz;  // Controlled_Buffer controlled_buffer_44
  assign PC_controll = and_13_out ? 3'b000 : 3'bz;  // Controlled_Buffer controlled_buffer_45
  assign mret = and_13_out ? 1'b0 : 1'bz;  // Controlled_Buffer controlled_buffer_46
  assign kehtiv_opcode = and_13_out ? 1'b1 : 1'bz;  // Controlled_Buffer controlled_buffer_47
  assign Write_enable = and_12_out ? 1'b0 : 1'bz;  // Controlled_Buffer controlled_buffer_48
  assign Data_type = and_12_out ? 3'b000 : 3'bz;  // Controlled_Buffer controlled_buffer_49
  assign ALU_src_A = and_12_out ? 1'b1 : 1'bz;  // Controlled_Buffer controlled_buffer_50
  assign Write_enable = and_13_out ? 1'b0 : 1'bz;  // Controlled_Buffer controlled_buffer_51
  assign Data_type = and_13_out ? 3'b000 : 3'bz;  // Controlled_Buffer controlled_buffer_52
  assign ALU_src_A = and_13_out ? 1'b0 : 1'bz;  // Controlled_Buffer controlled_buffer_53
  and and_14 (and_14_out, Juhis[0], Juhis[1], ~Juhis[2], ~Juhis[3], Juhis[4], ~Juhis[5], ~Juhis[6]);  // AND_Gate
  and and_15 (and_15_out, Juhis[0], Juhis[1], ~Juhis[2], ~Juhis[3], Juhis[4], ~Juhis[5], ~Juhis[6], ~Juhis[12], ~Juhis[13], ~Juhis[14]);  // AND_Gate
  and and_16 (and_16_out, Juhis[0], Juhis[1], ~Juhis[2], ~Juhis[3], Juhis[4], ~Juhis[5], ~Juhis[6], ~Juhis[12], Juhis[13], ~Juhis[14]);  // AND_Gate
  and and_17 (and_17_out, Juhis[0], Juhis[1], ~Juhis[2], ~Juhis[3], Juhis[4], ~Juhis[5], ~Juhis[6], Juhis[12], Juhis[13], ~Juhis[14]);  // AND_Gate
  and and_18 (and_18_out, Juhis[0], Juhis[1], ~Juhis[2], ~Juhis[3], Juhis[4], ~Juhis[5], ~Juhis[6], ~Juhis[12], ~Juhis[13], Juhis[14]);  // AND_Gate
  and and_19 (and_19_out, Juhis[0], Juhis[1], ~Juhis[2], ~Juhis[3], Juhis[4], ~Juhis[5], ~Juhis[6], ~Juhis[12], Juhis[13], Juhis[14]);  // AND_Gate
  and and_20 (and_20_out, Juhis[0], Juhis[1], ~Juhis[2], ~Juhis[3], Juhis[4], ~Juhis[5], ~Juhis[6], ~Juhis[12], Juhis[13], Juhis[14]);  // AND_Gate
  and and_21 (and_21_out, Juhis[0], Juhis[1], ~Juhis[2], ~Juhis[3], Juhis[4], ~Juhis[5], ~Juhis[6], Juhis[12], ~Juhis[13], ~Juhis[14]);  // AND_Gate
  and and_22 (and_22_out, Juhis[0], Juhis[1], ~Juhis[2], ~Juhis[3], Juhis[4], ~Juhis[5], ~Juhis[6], Juhis[12], ~Juhis[13], Juhis[14]);  // AND_Gate
  assign bit_extender_1_out = {{20{Juhis[31]}}, Juhis[31:20]};  // Bit_Extender bit_extender_1
  and and_23 (and_23_out, bit_extender_1_out[31], bit_extender_1_out[30], bit_extender_1_out[29], bit_extender_1_out[28], bit_extender_1_out[27]);
  and and_24 (and_24_out, and_23_out, and_22_out);
  and and_25 (and_25_out, bit_extender_1_out[31], bit_extender_1_out[30], bit_extender_1_out[29], ~bit_extender_1_out[28], bit_extender_1_out[27]);  // AND_Gate
  and and_26 (and_26_out, and_25_out, and_22_out);
  assign rd = and_14_out ? Juhis[11:7] : 5'bz;  // Controlled_Buffer controlled_buffer_54
  assign rs1 = and_14_out ? Juhis[19:15] : 5'bz;  // Controlled_Buffer controlled_buffer_55
  assign rs2 = and_14_out ? {5{1'b0}} : 5'bz;  // Controlled_Buffer controlled_buffer_56
  assign Immidiate = and_14_out ? bit_extender_1_out : 32'bz;  // Controlled_Buffer controlled_buffer_57
  assign ALU_src_A = and_14_out ? 1'b1 : 1'bz;  // Controlled_Buffer controlled_buffer_58
  assign Write_enable = and_14_out ? 1'b0 : 1'bz;  // Controlled_Buffer controlled_buffer_59
  assign Data_type = and_14_out ? 3'b000 : 3'bz;  // Controlled_Buffer controlled_buffer_60
  assign Register_mux = and_14_out ? 2'b10 : 2'bz;  // Controlled_Buffer controlled_buffer_61
  assign CSR_write_enable = and_14_out ? 1'b0 : 1'bz;  // Controlled_Buffer controlled_buffer_62
  assign ALU_src_B = and_14_out ? 1'b1 : 1'bz;  // Controlled_Buffer controlled_buffer_63
  assign CSR_address = and_14_out ? {12{1'b0}} : 12'bz;  // Controlled_Buffer controlled_buffer_64
  assign PC_controll = and_14_out ? 3'b000 : 3'bz;  // Controlled_Buffer controlled_buffer_65
  assign Branch_select = and_14_out ? 1'b0 : 1'bz;  // Controlled_Buffer controlled_buffer_66
  assign mret = and_14_out ? 1'b0 : 1'bz;  // Controlled_Buffer controlled_buffer_67
  assign kehtiv_opcode = and_14_out ? 1'b1 : 1'bz;  // Controlled_Buffer controlled_buffer_68
  assign Command = and_15_out ? {5{1'b0}} : 5'bz;  // Controlled_Buffer controlled_buffer_69
  assign Command = and_16_out ? 5'b10001 : 5'bz;  // Controlled_Buffer controlled_buffer_70
  assign Command = and_17_out ? 5'b00010 : 5'bz;  // Controlled_Buffer controlled_buffer_71
  assign Command = and_18_out ? 5'b01000 : 5'bz;  // Controlled_Buffer controlled_buffer_72
  assign Command = and_19_out ? 5'b00111 : 5'bz;  // Controlled_Buffer controlled_buffer_73
  assign Command = and_20_out ? 5'b00110 : 5'bz;  // Controlled_Buffer controlled_buffer_74
  assign Command = and_21_out ? 5'b00011 : 5'bz;  // Controlled_Buffer controlled_buffer_75
  assign Command = and_24_out ? 5'b00100 : 5'bz;  // Controlled_Buffer controlled_buffer_76
  assign Command = and_26_out ? 5'b00101 : 5'bz;  // Controlled_Buffer controlled_buffer_77
  and and_27 (and_27_out, Juhis[0], Juhis[1], ~Juhis[2], ~Juhis[3], Juhis[4], Juhis[5], Juhis[6]);  // AND_Gate
  or or_1 (or_1_out, Juhis[12], Juhis[13], Juhis[14]);
  and and_28 (and_28_out, Juhis[0], Juhis[1], ~Juhis[2], ~Juhis[3], Juhis[4], Juhis[5], Juhis[6], Juhis[12], ~Juhis[13], ~Juhis[14]);  // AND_Gate
  and and_29 (and_29_out, Juhis[0], Juhis[1], ~Juhis[2], ~Juhis[3], Juhis[4], Juhis[5], Juhis[6], ~Juhis[12], Juhis[13], ~Juhis[14]);  // AND_Gate
  and and_30 (and_30_out, Juhis[0], Juhis[1], ~Juhis[2], ~Juhis[3], Juhis[4], Juhis[5], Juhis[6], Juhis[12], Juhis[13], ~Juhis[14]);  // AND_Gate
  and and_31 (and_31_out, Juhis[0], Juhis[1], ~Juhis[2], ~Juhis[3], Juhis[4], Juhis[5], Juhis[6], Juhis[12], ~Juhis[13], Juhis[14]);  // AND_Gate
  and and_32 (and_32_out, Juhis[0], Juhis[1], ~Juhis[2], ~Juhis[3], Juhis[4], Juhis[5], Juhis[6], ~Juhis[12], Juhis[13], Juhis[14]);  // AND_Gate
  and and_33 (and_33_out, Juhis[0], Juhis[1], ~Juhis[2], ~Juhis[3], Juhis[4], Juhis[5], Juhis[6], Juhis[12], Juhis[13], Juhis[14]);  // AND_Gate
  and and_34 (and_34_out, and_27_out, or_1_out);
  assign bit_extender_2_out = {{27{1'b0}}, Juhis[24:20]};  // Bit_Extender bit_extender_2
  assign rd = and_34_out ? Juhis[11:7] : 5'bz;  // Controlled_Buffer controlled_buffer_78
  assign rs1 = and_34_out ? Juhis[19:15] : 5'bz;  // Controlled_Buffer controlled_buffer_79
  assign rs2 = and_34_out ? {5{1'b0}} : 5'bz;  // Controlled_Buffer controlled_buffer_80
  assign CSR_address = and_34_out ? Juhis[31:20] : 12'bz;  // Controlled_Buffer controlled_buffer_81
  assign Immidiate = and_34_out ? bit_extender_2_out : 32'bz;  // Controlled_Buffer controlled_buffer_82
  assign ALU_src_A = and_34_out ? 1'b1 : 1'bz;  // Controlled_Buffer controlled_buffer_83
  assign CSR_write_enable = and_34_out ? 1'b1 : 1'bz;  // Controlled_Buffer controlled_buffer_84
  assign Write_enable = and_34_out ? 1'b0 : 1'bz;  // Controlled_Buffer controlled_buffer_85
  assign Data_type = and_34_out ? 3'b000 : 3'bz;  // Controlled_Buffer controlled_buffer_86
  assign Register_mux = and_34_out ? 2'b01 : 2'bz;  // Controlled_Buffer controlled_buffer_87
  assign PC_controll = and_34_out ? 3'b000 : 3'bz;  // Controlled_Buffer controlled_buffer_88
  assign mret = and_34_out ? 1'b0 : 1'bz;  // Controlled_Buffer controlled_buffer_89
  assign kehtiv_opcode = and_34_out ? 1'b1 : 1'bz;  // Controlled_Buffer controlled_buffer_90
  assign Command = and_28_out ? {5{1'b0}} : 5'bz;  // Controlled_Buffer controlled_buffer_91
  assign ALU_src_B = and_28_out ? 1'b0 : 1'bz;  // Controlled_Buffer controlled_buffer_92
  assign Command = and_29_out ? 5'b00111 : 5'bz;  // Controlled_Buffer controlled_buffer_93
  assign ALU_src_B = and_29_out ? 1'b0 : 1'bz;  // Controlled_Buffer controlled_buffer_94
  assign Command = and_30_out ? 5'b01000 : 5'bz;  // Controlled_Buffer controlled_buffer_95
  assign ALU_src_B = and_30_out ? 1'b0 : 1'bz;  // Controlled_Buffer controlled_buffer_96
  assign Command = and_31_out ? {5{1'b0}} : 5'bz;  // Controlled_Buffer controlled_buffer_97
  assign ALU_src_B = and_31_out ? 1'b1 : 1'bz;  // Controlled_Buffer controlled_buffer_98
  assign Command = and_32_out ? 5'b00111 : 5'bz;  // Controlled_Buffer controlled_buffer_99
  assign ALU_src_B = and_32_out ? 1'b1 : 1'bz;  // Controlled_Buffer controlled_buffer_100
  assign Command = and_33_out ? 5'b01000 : 5'bz;  // Controlled_Buffer controlled_buffer_101
  assign ALU_src_B = and_33_out ? 1'b1 : 1'bz;  // Controlled_Buffer controlled_buffer_102
  assign bit_extender_3_out = {{11{Juhis[31]}}, Juhis[31]};  // Bit_Extender bit_extender_3
  and and_35 (and_35_out, Juhis[0], Juhis[1], Juhis[2], Juhis[3], ~Juhis[4], Juhis[5], Juhis[6]);  // AND_Gate
  and and_36 (and_36_out, Juhis[0], Juhis[1], Juhis[2], ~Juhis[3], ~Juhis[4], Juhis[5], Juhis[6], ~Juhis[12], ~Juhis[13], ~Juhis[14]);  // AND_Gate
  assign bit_extender_4_out = {{20{Juhis[31]}}, Juhis[31:20]};  // Bit_Extender bit_extender_4
  assign Immidiate = and_35_out ? {bit_extender_3_out, Juhis[19:12], Juhis[20], Juhis[30:21], 1'b0} : 32'bz;  // Controlled_Buffer controlled_buffer_103
  assign Command = and_35_out ? {5{1'b0}} : 5'bz;  // Controlled_Buffer controlled_buffer_104
  assign Register_mux = and_35_out ? 2'b00 : 2'bz;  // Controlled_Buffer controlled_buffer_105
  assign ALU_src_A = and_35_out ? 1'b0 : 1'bz;  // Controlled_Buffer controlled_buffer_106
  assign rs1 = and_35_out ? {5{1'b0}} : 5'bz;  // Controlled_Buffer controlled_buffer_107
  assign rs2 = and_35_out ? {5{1'b0}} : 5'bz;  // Controlled_Buffer controlled_buffer_108
  assign rd = and_35_out ? Juhis[11:7] : 5'bz;  // Controlled_Buffer controlled_buffer_109
  assign Data_type = and_35_out ? 3'b000 : 3'bz;  // Controlled_Buffer controlled_buffer_110
  assign ALU_src_B = and_35_out ? 1'b1 : 1'bz;  // Controlled_Buffer controlled_buffer_111
  assign Write_enable = and_35_out ? 1'b0 : 1'bz;  // Controlled_Buffer controlled_buffer_112
  assign CSR_write_enable = and_35_out ? 1'b0 : 1'bz;  // Controlled_Buffer controlled_buffer_113
  assign CSR_address = and_35_out ? {12{1'b0}} : 12'bz;  // Controlled_Buffer controlled_buffer_114
  assign PC_controll = and_35_out ? 3'b001 : 3'bz;  // Controlled_Buffer controlled_buffer_115
  assign mret = and_35_out ? 1'b0 : 1'bz;  // Controlled_Buffer controlled_buffer_116
  assign kehtiv_opcode = and_35_out ? 1'b1 : 1'bz;  // Controlled_Buffer controlled_buffer_117
  assign Immidiate = and_36_out ? bit_extender_4_out : 32'bz;  // Controlled_Buffer controlled_buffer_118
  assign Command = and_36_out ? {5{1'b0}} : 5'bz;  // Controlled_Buffer controlled_buffer_119
  assign Register_mux = and_36_out ? 2'b00 : 2'bz;  // Controlled_Buffer controlled_buffer_120
  assign ALU_src_A = and_36_out ? 1'b1 : 1'bz;  // Controlled_Buffer controlled_buffer_121
  assign rs1 = and_36_out ? Juhis[19:15] : 5'bz;  // Controlled_Buffer controlled_buffer_122
  assign rs2 = and_36_out ? {5{1'b0}} : 5'bz;  // Controlled_Buffer controlled_buffer_123
  assign rd = and_36_out ? Juhis[11:7] : 5'bz;  // Controlled_Buffer controlled_buffer_124
  assign Data_type = and_36_out ? 3'b000 : 3'bz;  // Controlled_Buffer controlled_buffer_125
  assign ALU_src_B = and_36_out ? 1'b1 : 1'bz;  // Controlled_Buffer controlled_buffer_126
  assign Write_enable = and_36_out ? 1'b0 : 1'bz;  // Controlled_Buffer controlled_buffer_127
  assign CSR_write_enable = and_36_out ? 1'b0 : 1'bz;  // Controlled_Buffer controlled_buffer_128
  assign CSR_address = and_36_out ? {12{1'b0}} : 12'bz;  // Controlled_Buffer controlled_buffer_129
  assign PC_controll = and_36_out ? 3'b001 : 3'bz;  // Controlled_Buffer controlled_buffer_130
  assign mret = and_36_out ? 1'b0 : 1'bz;  // Controlled_Buffer controlled_buffer_131
  assign kehtiv_opcode = and_36_out ? 1'b1 : 1'bz;  // Controlled_Buffer controlled_buffer_132
  and and_37 (and_37_out, Juhis[0], Juhis[1], ~Juhis[2], ~Juhis[3], ~Juhis[4], Juhis[5], Juhis[6]);  // AND_Gate
  assign bit_extender_5_out = {{19{Juhis[31]}}, {Juhis[31], Juhis[7], Juhis[30:25], Juhis[11:8], 1'b0}};  // Bit_Extender bit_extender_5
  and and_38 (and_38_out, and_37_out, ~Juhis[12], ~Juhis[13], ~Juhis[14]);  // AND_Gate
  and and_39 (and_39_out, and_37_out, Juhis[12], ~Juhis[13], ~Juhis[14]);  // AND_Gate
  and and_40 (and_40_out, and_37_out, ~Juhis[12], ~Juhis[13], Juhis[14]);  // AND_Gate
  and and_41 (and_41_out, and_37_out, Juhis[12], ~Juhis[13], Juhis[14]);  // AND_Gate
  and and_42 (and_42_out, and_37_out, ~Juhis[12], Juhis[13], Juhis[14]);  // AND_Gate
  and and_43 (and_43_out, and_37_out, Juhis[12], Juhis[13], Juhis[14]);
  assign Immidiate = and_37_out ? bit_extender_5_out : 32'bz;  // Controlled_Buffer controlled_buffer_133
  assign Register_mux = and_37_out ? 2'b00 : 2'bz;  // Controlled_Buffer controlled_buffer_134
  assign ALU_src_A = and_37_out ? 1'b0 : 1'bz;  // Controlled_Buffer controlled_buffer_135
  assign rs1 = and_37_out ? Juhis[19:15] : 5'bz;  // Controlled_Buffer controlled_buffer_136
  assign rs2 = and_37_out ? Juhis[24:20] : 5'bz;  // Controlled_Buffer controlled_buffer_137
  assign rd = and_37_out ? {5{1'b0}} : 5'bz;  // Controlled_Buffer controlled_buffer_138
  assign Data_type = and_37_out ? 3'b000 : 3'bz;  // Controlled_Buffer controlled_buffer_139
  assign ALU_src_B = and_37_out ? 1'b1 : 1'bz;  // Controlled_Buffer controlled_buffer_140
  assign Write_enable = and_37_out ? 1'b0 : 1'bz;  // Controlled_Buffer controlled_buffer_141
  assign CSR_write_enable = and_37_out ? 1'b0 : 1'bz;  // Controlled_Buffer controlled_buffer_142
  assign CSR_address = and_37_out ? {12{1'b0}} : 12'bz;  // Controlled_Buffer controlled_buffer_143
  assign PC_controll = and_37_out ? 3'b100 : 3'bz;  // Controlled_Buffer controlled_buffer_144
  assign mret = and_37_out ? 1'b0 : 1'bz;  // Controlled_Buffer controlled_buffer_145
  assign kehtiv_opcode = and_37_out ? 1'b1 : 1'bz;  // Controlled_Buffer controlled_buffer_146
  assign Branch_select = and_38_out ? 1'b1 : 1'bz;  // Controlled_Buffer controlled_buffer_147
  assign Command = and_38_out ? 5'b01001 : 5'bz;  // Controlled_Buffer controlled_buffer_148
  assign Branch_select = and_39_out ? 1'b0 : 1'bz;  // Controlled_Buffer controlled_buffer_149
  assign Command = and_39_out ? 5'b01001 : 5'bz;  // Controlled_Buffer controlled_buffer_150
  assign Branch_select = and_40_out ? 1'b0 : 1'bz;  // Controlled_Buffer controlled_buffer_151
  assign Command = and_40_out ? 5'b10001 : 5'bz;  // Controlled_Buffer controlled_buffer_152
  assign Branch_select = and_41_out ? 1'b1 : 1'bz;  // Controlled_Buffer controlled_buffer_153
  assign Command = and_41_out ? 5'b10001 : 5'bz;  // Controlled_Buffer controlled_buffer_154
  assign Branch_select = and_42_out ? 1'b0 : 1'bz;  // Controlled_Buffer controlled_buffer_155
  assign Command = and_42_out ? 5'b00010 : 5'bz;  // Controlled_Buffer controlled_buffer_156
  assign Branch_select = and_43_out ? 1'b1 : 1'bz;  // Controlled_Buffer controlled_buffer_157
  assign Command = and_43_out ? 5'b00010 : 5'bz;  // Controlled_Buffer controlled_buffer_158
  and and_44 (and_44_out, Juhis[0], Juhis[1], ~Juhis[2], ~Juhis[3], Juhis[4], Juhis[5], Juhis[6], ~Juhis[7], ~Juhis[8], ~Juhis[9], ~Juhis[10], ~Juhis[11], ~Juhis[12], ~Juhis[13], ~Juhis[14], ~Juhis[15], ~Juhis[17], ~Juhis[18], ~Juhis[19], Juhis[20], ~Juhis[21], Juhis[22], ~Juhis[23], ~Juhis[24], ~Juhis[25], ~Juhis[26], ~Juhis[27], Juhis[28], ~Juhis[29], ~Juhis[30], ~Juhis[31], ~Juhis[16]);  // AND_Gate
  and and_45 (and_45_out, Juhis[0], Juhis[1], ~Juhis[2], ~Juhis[3], Juhis[4], Juhis[5], Juhis[6], ~Juhis[7], ~Juhis[8], ~Juhis[9], ~Juhis[10], ~Juhis[11], ~Juhis[12], ~Juhis[13], ~Juhis[14], ~Juhis[15], ~Juhis[17], ~Juhis[18], ~Juhis[19], ~Juhis[20], ~Juhis[21], ~Juhis[22], ~Juhis[23], ~Juhis[24], ~Juhis[25], ~Juhis[26], ~Juhis[27], ~Juhis[28], ~Juhis[29], ~Juhis[30], ~Juhis[31], ~Juhis[16]);  // AND_Gate
  and and_46 (and_46_out, Juhis[0], Juhis[1], ~Juhis[2], ~Juhis[3], Juhis[4], Juhis[5], Juhis[6], ~Juhis[7], ~Juhis[8], ~Juhis[9], ~Juhis[10], ~Juhis[11], ~Juhis[12], ~Juhis[13], ~Juhis[14], ~Juhis[15], ~Juhis[17], ~Juhis[18], ~Juhis[19], Juhis[20], ~Juhis[21], ~Juhis[22], ~Juhis[23], ~Juhis[24], ~Juhis[25], ~Juhis[26], ~Juhis[27], ~Juhis[28], ~Juhis[29], ~Juhis[30], ~Juhis[31], ~Juhis[16]);  // AND_Gate
  assign kehtiv_opcode = and_44_out ? 1'b1 : 1'bz;  // Controlled_Buffer controlled_buffer_159
  assign Immidiate = and_44_out ? {32{1'b0}} : 32'bz;  // Controlled_Buffer controlled_buffer_160
  assign Register_mux = and_44_out ? 2'b00 : 2'bz;  // Controlled_Buffer controlled_buffer_161
  assign ALU_src_A = and_44_out ? 1'b0 : 1'bz;  // Controlled_Buffer controlled_buffer_162
  assign rs1 = and_44_out ? {5{1'b0}} : 5'bz;  // Controlled_Buffer controlled_buffer_163
  assign rs2 = and_44_out ? {5{1'b0}} : 5'bz;  // Controlled_Buffer controlled_buffer_164
  assign rd = and_44_out ? {5{1'b0}} : 5'bz;  // Controlled_Buffer controlled_buffer_165
  assign Data_type = and_44_out ? 3'b000 : 3'bz;  // Controlled_Buffer controlled_buffer_166
  assign ALU_src_B = and_44_out ? 1'b1 : 1'bz;  // Controlled_Buffer controlled_buffer_167
  assign Write_enable = and_44_out ? 1'b0 : 1'bz;  // Controlled_Buffer controlled_buffer_168
  assign CSR_write_enable = and_44_out ? 1'b0 : 1'bz;  // Controlled_Buffer controlled_buffer_169
  assign CSR_address = and_44_out ? {12{1'b0}} : 12'bz;  // Controlled_Buffer controlled_buffer_170
  assign PC_controll = and_44_out ? 3'b010 : 3'bz;  // Controlled_Buffer controlled_buffer_171
  assign Branch_select = and_44_out ? 1'b0 : 1'bz;  // Controlled_Buffer controlled_buffer_172
  assign Command = and_44_out ? 5'b01001 : 5'bz;  // Controlled_Buffer controlled_buffer_173
  assign kehtiv_opcode = and_45_out ? 1'b1 : 1'bz;  // Controlled_Buffer controlled_buffer_174
  assign Immidiate = and_45_out ? {32{1'b0}} : 32'bz;  // Controlled_Buffer controlled_buffer_175
  assign Register_mux = and_45_out ? 2'b00 : 2'bz;  // Controlled_Buffer controlled_buffer_176
  assign ALU_src_A = and_45_out ? 1'b0 : 1'bz;  // Controlled_Buffer controlled_buffer_177
  assign rs1 = and_45_out ? {5{1'b0}} : 5'bz;  // Controlled_Buffer controlled_buffer_178
  assign rs2 = and_45_out ? {5{1'b0}} : 5'bz;  // Controlled_Buffer controlled_buffer_179
  assign rd = and_45_out ? {5{1'b0}} : 5'bz;  // Controlled_Buffer controlled_buffer_180
  assign Data_type = and_45_out ? 3'b000 : 3'bz;  // Controlled_Buffer controlled_buffer_181
  assign ALU_src_B = and_45_out ? 1'b1 : 1'bz;  // Controlled_Buffer controlled_buffer_182
  assign Write_enable = and_45_out ? 1'b0 : 1'bz;  // Controlled_Buffer controlled_buffer_183
  assign CSR_write_enable = and_45_out ? 1'b0 : 1'bz;  // Controlled_Buffer controlled_buffer_184
  assign CSR_address = and_45_out ? {12{1'b0}} : 12'bz;  // Controlled_Buffer controlled_buffer_185
  assign PC_controll = and_45_out ? 3'b010 : 3'bz;  // Controlled_Buffer controlled_buffer_186
  assign Branch_select = and_45_out ? 1'b0 : 1'bz;  // Controlled_Buffer controlled_buffer_187
  assign Command = and_45_out ? 5'b01001 : 5'bz;  // Controlled_Buffer controlled_buffer_188
  assign mret = and_45_out ? 1'b1 : 1'bz;  // Controlled_Buffer controlled_buffer_189
  assign Immidiate = and_46_out ? {32{1'b0}} : 32'bz;  // Controlled_Buffer controlled_buffer_190
  assign Register_mux = and_46_out ? 2'b00 : 2'bz;  // Controlled_Buffer controlled_buffer_191
  assign ALU_src_A = and_46_out ? 1'b0 : 1'bz;  // Controlled_Buffer controlled_buffer_192
  assign rs1 = and_46_out ? {5{1'b0}} : 5'bz;  // Controlled_Buffer controlled_buffer_193
  assign rs2 = and_46_out ? {5{1'b0}} : 5'bz;  // Controlled_Buffer controlled_buffer_194
  assign rd = and_46_out ? {5{1'b0}} : 5'bz;  // Controlled_Buffer controlled_buffer_195
  assign Data_type = and_46_out ? 3'b000 : 3'bz;  // Controlled_Buffer controlled_buffer_196
  assign ALU_src_B = and_46_out ? 1'b1 : 1'bz;  // Controlled_Buffer controlled_buffer_197
  assign Write_enable = and_46_out ? 1'b0 : 1'bz;  // Controlled_Buffer controlled_buffer_198
  assign CSR_write_enable = and_46_out ? 1'b0 : 1'bz;  // Controlled_Buffer controlled_buffer_199
  assign CSR_address = and_46_out ? {12{1'b0}} : 12'bz;  // Controlled_Buffer controlled_buffer_200
  assign PC_controll = and_46_out ? 3'b010 : 3'bz;  // Controlled_Buffer controlled_buffer_201
  assign Branch_select = and_46_out ? 1'b0 : 1'bz;  // Controlled_Buffer controlled_buffer_202
  assign Command = and_46_out ? 5'b01001 : 5'bz;  // Controlled_Buffer controlled_buffer_203
  assign mret = and_46_out ? 1'b0 : 1'bz;  // Controlled_Buffer controlled_buffer_204
  assign kehtiv_opcode = and_46_out ? 1'b1 : 1'bz;  // Controlled_Buffer controlled_buffer_205
  assign bit_extender_6_out = {{20{Juhis[31]}}, {Juhis[31:25], Juhis[11:7]}};  // Bit_Extender bit_extender_6
  and and_47 (and_47_out, Juhis[0], Juhis[1], ~Juhis[2], ~Juhis[3], ~Juhis[4], Juhis[5], ~Juhis[6]);  // AND_Gate
  and and_48 (and_48_out, and_47_out, ~Juhis[12], ~Juhis[13], ~Juhis[14]);  // AND_Gate
  and and_49 (and_49_out, and_47_out, Juhis[12], ~Juhis[13], ~Juhis[14]);  // AND_Gate
  and and_50 (and_50_out, and_47_out, ~Juhis[12], Juhis[13], ~Juhis[14]);  // AND_Gate
  assign Immidiate = and_47_out ? bit_extender_6_out : 32'bz;  // Controlled_Buffer controlled_buffer_206
  assign Register_mux = and_47_out ? 2'b00 : 2'bz;  // Controlled_Buffer controlled_buffer_207
  assign ALU_src_A = and_47_out ? 1'b1 : 1'bz;  // Controlled_Buffer controlled_buffer_208
  assign rs1 = and_47_out ? Juhis[19:15] : 5'bz;  // Controlled_Buffer controlled_buffer_209
  assign rs2 = and_47_out ? Juhis[24:20] : 5'bz;  // Controlled_Buffer controlled_buffer_210
  assign rd = and_47_out ? {5{1'b0}} : 5'bz;  // Controlled_Buffer controlled_buffer_211
  assign Command = and_47_out ? {5{1'b0}} : 5'bz;  // Controlled_Buffer controlled_buffer_212
  assign ALU_src_B = and_47_out ? 1'b1 : 1'bz;  // Controlled_Buffer controlled_buffer_213
  assign Write_enable = and_47_out ? 1'b1 : 1'bz;  // Controlled_Buffer controlled_buffer_214
  assign CSR_write_enable = and_47_out ? 1'b0 : 1'bz;  // Controlled_Buffer controlled_buffer_215
  assign CSR_address = and_47_out ? {12{1'b0}} : 12'bz;  // Controlled_Buffer controlled_buffer_216
  assign PC_controll = and_47_out ? 3'b000 : 3'bz;  // Controlled_Buffer controlled_buffer_217
  assign Branch_select = and_47_out ? 1'b0 : 1'bz;  // Controlled_Buffer controlled_buffer_218
  assign mret = and_47_out ? 1'b0 : 1'bz;  // Controlled_Buffer controlled_buffer_219
  assign kehtiv_opcode = and_47_out ? 1'b1 : 1'bz;  // Controlled_Buffer controlled_buffer_220
  assign Data_type = and_48_out ? 3'b111 : 3'bz;  // Controlled_Buffer controlled_buffer_221
  assign Data_type = and_49_out ? 3'b110 : 3'bz;  // Controlled_Buffer controlled_buffer_222
  assign Data_type = and_50_out ? 3'b101 : 3'bz;  // Controlled_Buffer controlled_buffer_223
  assign bit_extender_7_out = {{20{Juhis[31]}}, Juhis[31:20]};  // Bit_Extender bit_extender_7
  and and_51 (and_51_out, Juhis[0], Juhis[1], ~Juhis[2], ~Juhis[3], ~Juhis[4], ~Juhis[5], ~Juhis[6]);  // AND_Gate
  assign kehtiv_opcode = and_51_out ? 1'b1 : 1'bz;  // Controlled_Buffer controlled_buffer_224
  and and_52 (and_52_out, and_51_out, ~Juhis[12], ~Juhis[13], ~Juhis[14]);  // AND_Gate
  and and_53 (and_53_out, and_51_out, Juhis[12], ~Juhis[13], ~Juhis[14]);  // AND_Gate
  and and_54 (and_54_out, and_51_out, ~Juhis[12], Juhis[13], ~Juhis[14]);  // AND_Gate
  and and_55 (and_55_out, and_51_out, ~Juhis[12], ~Juhis[13], Juhis[14]);  // AND_Gate
  and and_56 (and_56_out, and_51_out, Juhis[12], ~Juhis[13], Juhis[14]);  // AND_Gate
  assign Immidiate = and_51_out ? bit_extender_7_out : 32'bz;  // Controlled_Buffer controlled_buffer_225
  assign Register_mux = and_51_out ? 2'b11 : 2'bz;  // Controlled_Buffer controlled_buffer_226
  assign ALU_src_A = and_51_out ? 1'b1 : 1'bz;  // Controlled_Buffer controlled_buffer_227
  assign rs1 = and_51_out ? Juhis[19:15] : 5'bz;  // Controlled_Buffer controlled_buffer_228
  assign rs2 = and_51_out ? {5{1'b0}} : 5'bz;  // Controlled_Buffer controlled_buffer_229
  assign rd = and_51_out ? Juhis[11:7] : 5'bz;  // Controlled_Buffer controlled_buffer_230
  assign Command = and_51_out ? {5{1'b0}} : 5'bz;  // Controlled_Buffer controlled_buffer_231
  assign ALU_src_B = and_51_out ? 1'b1 : 1'bz;  // Controlled_Buffer controlled_buffer_232
  assign Write_enable = and_51_out ? 1'b0 : 1'bz;  // Controlled_Buffer controlled_buffer_233
  assign CSR_write_enable = and_51_out ? 1'b0 : 1'bz;  // Controlled_Buffer controlled_buffer_234
  assign CSR_address = and_51_out ? {12{1'b0}} : 12'bz;  // Controlled_Buffer controlled_buffer_235
  assign PC_controll = and_51_out ? 3'b000 : 3'bz;  // Controlled_Buffer controlled_buffer_236
  assign Branch_select = and_51_out ? 1'b1 : 1'bz;  // Controlled_Buffer controlled_buffer_237
  assign mret = and_51_out ? 1'b0 : 1'bz;  // Controlled_Buffer controlled_buffer_238
  assign Data_type = and_52_out ? 3'b011 : 3'bz;  // Controlled_Buffer controlled_buffer_239
  assign Data_type = and_53_out ? 3'b001 : 3'bz;  // Controlled_Buffer controlled_buffer_240
  assign Data_type = and_54_out ? 3'b000 : 3'bz;  // Controlled_Buffer controlled_buffer_241
  assign Data_type = and_55_out ? 3'b100 : 3'bz;  // Controlled_Buffer controlled_buffer_242
  assign Data_type = and_56_out ? 3'b010 : 3'bz;  // Controlled_Buffer controlled_buffer_243
  Pull_Resistor pull_resistor_1 (.node(mret));
  Pull_Resistor pull_resistor_2 (.node(kehtiv_opcode));

  // Other names for the same wires on the sheet: kehtiv = kehtiv_opcode; PC_ctrl[2:0] = PC_controll

  // Notes on the sheet:
  //   mret: pull=down
  //   kehtiv_opcode: pull=down
  //   ADD
  //   SUB
  //   AND
  //   OR
  //   XOR
  //   SLL
  //   SLT
  //   SLT
  //   SRL
  //   SRA
  //   R type
  //   LUI
  //   AUIPC
  //   U type
  //   ADDI
  //   SLTI
  //   SLTIU
  //   XORI
  //   ORI
  //   ANDI
  //   SLLI
  //   SRLI
  //   SRAI
  //   I type
  //   I type CSR
  //   CSRRW
  //   CSRRS
  //   CSRRC
  //   CSRRWI
  //   CSRRSI
  //   CSRRCI
  //   JAL
  //   JALR
  //   Jumps
  //   BEQ
  //   BNE
  //   BLT
  //   BGE
  //   BLTU
  //   BGEU
  //   B type (branch)
  //   WFI
  //   ECALL
  //   EBREAK
  //   Store
  //   SB
  //   SH
  //   SW
  //   Malu kasud
  //   Load
  //   LB
  //   LH
  //   LW
  //   LBU
  //   LHU
endmodule

module Microcontroller (
);

  wire aadressi_vordleja_1_out_3, aadressi_vordleja_2_out_3, aadressi_vordleja_3_out_3,
       aadressi_vordleja_4_out_3, and_1_out, and_2_out, and_3_out, and_4_out, and_5_out, button_1_out,
       clock_1_out, cpu_1_kirjuta_mallu, nor_1_out, t_ff_1_q, taimer_1_puhastus, taimer_1_valjasta_signaal;
  wire [2:0] pull_resistor_2_node;
  wire [3:0] timer_adv_1_viigud_valja;
  wire [5:5] PB_p4;
  wire [7:0] timer_adv_1_erandid;
  wire [19:0] taimer_1_ulevoolu_katkestus;
  wire [29:1] pull_resistor_2_node_2;
  wire [31:0] and_6_out, and_7_out, and_8_out, and_9_out, and_10_out, and_11_out, controlled_buffer_1_out,
       cpu_1_alu_valjund, cpu_1_juhise_aadress, cpu_1_malu_valjund, or_1_out, or_2_out, pull_resistor_1_node,
       ram_1_dout, register_1_q, register_2_q, register_3_q, register_4_q, rom_1_data;

  // Probe on cpu_1_juhise_aadress[31:18]
  // Probe on cpu_1_juhise_aadress[1:0]
  ROM #(.addrWidth(16), .dataWidth(32)) rom_1 (.addr(cpu_1_juhise_aadress[17:2]), .data(rom_1_data));
  Button button_1 (.out(button_1_out));
  Clock clock_1 (.out(clock_1_out));
  CPU cpu_1 (
    .juhis(rom_1_data), .malu_sisend(controlled_buffer_1_out), .reset(button_1_out), .clk(clock_1_out),
    .Ext_Interrupt(taimer_1_ulevoolu_katkestus), .juhise_aadress(cpu_1_juhise_aadress),
    .ALU_valjund(cpu_1_alu_valjund), .kirjuta_mallu(cpu_1_kirjuta_mallu), .malu_valjund(cpu_1_malu_valjund));
  nor nor_1 (nor_1_out, ~cpu_1_alu_valjund[14], cpu_1_alu_valjund[15], cpu_1_alu_valjund[16], cpu_1_alu_valjund[17], cpu_1_alu_valjund[18], cpu_1_alu_valjund[19], cpu_1_alu_valjund[20], cpu_1_alu_valjund[21], cpu_1_alu_valjund[22], cpu_1_alu_valjund[24], cpu_1_alu_valjund[25], cpu_1_alu_valjund[26], cpu_1_alu_valjund[27], cpu_1_alu_valjund[28], cpu_1_alu_valjund[29], cpu_1_alu_valjund[30], cpu_1_alu_valjund[31], cpu_1_alu_valjund[23]);  // NOR_Gate
  and and_1 (and_1_out, cpu_1_kirjuta_mallu, nor_1_out);
  RAM #(.addrWidth(12), .dataWidth(32), .enables("line")) ram_1 (
    .addr(cpu_1_alu_valjund[13:2]), .we(and_1_out), .clk(clock_1_out), .din(cpu_1_malu_valjund),
    .dout(ram_1_dout));
  assign controlled_buffer_1_out = nor_1_out ? ram_1_dout : 32'bz;  // Controlled_Buffer controlled_buffer_1
  // Probe on cpu_1_alu_valjund
  aadressi_vordleja aadressi_vordleja_1 (
    .in_1(cpu_1_alu_valjund), .in_2({32{1'b0}}), .out_3(aadressi_vordleja_1_out_3));
  aadressi_vordleja aadressi_vordleja_2 (.in_1(cpu_1_alu_valjund), .in_2(32'h4), .out_3(aadressi_vordleja_2_out_3));
  aadressi_vordleja aadressi_vordleja_3 (.in_1(cpu_1_alu_valjund), .in_2(32'h14), .out_3(aadressi_vordleja_3_out_3));
  aadressi_vordleja aadressi_vordleja_4 (.in_1(cpu_1_alu_valjund), .in_2(32'h18), .out_3(aadressi_vordleja_4_out_3));
  // Probe on cpu_1_alu_valjund
  Register #(.width(32)) register_1 (
    .D(cpu_1_malu_valjund), .en(and_2_out), .clk(clock_1_out), .Q(register_1_q));  // open: clr
  and and_2 (and_2_out, cpu_1_kirjuta_mallu, aadressi_vordleja_1_out_3);
  Register #(.width(32)) register_2 (
    .D(cpu_1_malu_valjund), .en(and_3_out), .clk(clock_1_out), .Q(register_2_q));  // open: clr
  and and_3 (and_3_out, cpu_1_kirjuta_mallu, aadressi_vordleja_2_out_3);
  Register #(.width(32)) register_3 (
    .D(cpu_1_malu_valjund), .en(and_4_out), .clk(clock_1_out), .Q(register_3_q));  // open: clr
  and and_4 (and_4_out, cpu_1_kirjuta_mallu, aadressi_vordleja_3_out_3);
  Register #(.width(32)) register_4 (
    .D(cpu_1_malu_valjund), .en(and_5_out), .clk(clock_1_out), .Q(register_4_q));  // open: clr
  and and_5 (and_5_out, cpu_1_kirjuta_mallu, aadressi_vordleja_4_out_3);
  assign controlled_buffer_1_out = aadressi_vordleja_2_out_3 ? register_2_q : 32'bz;  // Controlled_Buffer controlled_buffer_2
  assign controlled_buffer_1_out = aadressi_vordleja_4_out_3 ? register_4_q : 32'bz;  // Controlled_Buffer controlled_buffer_3
  assign controlled_buffer_1_out = aadressi_vordleja_1_out_3 ? or_1_out : 32'bz;  // Controlled_Buffer controlled_buffer_4
  assign or_1_out = and_6_out | and_8_out;  // OR_Gate or_1, 32 bits wide
  assign and_6_out = register_2_q & register_1_q;  // AND_Gate and_6, 32 bits wide
  assign controlled_buffer_1_out = aadressi_vordleja_3_out_3 ? or_2_out : 32'bz;  // Controlled_Buffer controlled_buffer_5
  assign or_2_out = and_7_out | and_9_out;  // OR_Gate or_2, 32 bits wide
  assign and_7_out = register_4_q & register_3_q;  // AND_Gate and_7, 32 bits wide
  assign and_8_out = ~register_2_q & pull_resistor_1_node;  // AND_Gate and_8, 32 bits wide
  Pull_Resistor pull_resistor_1 (.node(pull_resistor_1_node));
  // PortIO #(.direction("IOMultiEnable"), .number(32)) PA: pin names not known; wires that end beside it: and_2_out, and_3_out, register_1_q, pull_resistor_1_node
  Timer_adv timer_adv_1 (
    .Andmed_sisse(cpu_1_malu_valjund), .Malu_aadress(cpu_1_alu_valjund), .TMR_ADDR(32'h1014),
    .Luba_kirjutamine(cpu_1_kirjuta_mallu), .CLK(clock_1_out), .Andmed_valja(controlled_buffer_1_out),
    .Erandid(timer_adv_1_erandid), .Viigud_valja(timer_adv_1_viigud_valja));  // open: Viigud_sisse
  Taimer taimer_1 (
    .CLK(clock_1_out), .Maluaadress(cpu_1_malu_valjund), .Luba_kirjutamine(cpu_1_kirjuta_mallu),
    .lugemise_suund(pull_resistor_2_node_2[29]), .MA_kontroll(32'h8), .MA_algvaartus(32'hc),
    .MA_vordlus(32'h10), .Valine_kellasisend(pull_resistor_2_node), .Valjund(controlled_buffer_1_out),
    .ulevoolu_katkestus(taimer_1_ulevoolu_katkestus[0]), .vordlus_katkestus(taimer_1_ulevoolu_katkestus[1]),
    .Puhastus(taimer_1_puhastus), .valjasta_signaal(taimer_1_valjasta_signaal));
  assign and_9_out = ~register_4_q & {pull_resistor_2_node[2:1], pull_resistor_2_node_2, pull_resistor_2_node[0]};  // AND_Gate and_9, 32 bits wide
  // PortIO #(.direction("IOMultiEnable"), .number(32)) PB: pin names not known; wires that end beside it: and_4_out, and_5_out, register_4_q, {register_3_q[31:6], PB_p4[5], register_3_q[4:0]}
  T_Flip_Flop t_ff_1 (.T(taimer_1_puhastus), .clk(clock_1_out), .Q(t_ff_1_q));  // open: Qn, reset, preset
  Multiplexer multiplexer_1 (.in0(register_3_q[5]), .in1(t_ff_1_q), .out(PB_p4[5]), .sel(taimer_1_valjasta_signaal));
  // Probe on timer_adv_1_erandid
  // Probe on timer_adv_1_viigud_valja
  Pull_Resistor pull_resistor_2 (.node({pull_resistor_2_node[2:1], pull_resistor_2_node_2, pull_resistor_2_node[0]}));
  assign and_10_out = register_3_q & ~register_4_q;  // AND_Gate and_10, 32 bits wide
  assign {and_11_out[31:3], taimer_1_ulevoolu_katkestus[3:2], and_11_out[0]} = {pull_resistor_2_node[2:1], pull_resistor_2_node_2, pull_resistor_2_node[0]} & and_10_out;  // AND_Gate and_11, 32 bits wide

  // Notes on the sheet:
  //   contents of rom_1 (hex, n*v repeats v):
  //   12b7 1428293 a00313 62a423 20000337 4130313 62a023 6f 517 4050513 593 613 c50c63 52283 55a023 450513
  //   458593 fedff06f 513 593 fab508e3 52023 450513 ff5ff06f
  //   0 - sisend
  //   1 - valjund
endmodule

module aadressi_vordleja (
  input  [31:0] in_1,
  input  [31:0] in_2,
  output out_3
);

  wire [31:0] xnor_1_out;

  assign xnor_1_out = ~(in_1 ^ in_2);  // XNOR_Gate xnor_1, 32 bits wide
  and and_1 (out_3, xnor_1_out[16], xnor_1_out[2], xnor_1_out[3], xnor_1_out[4], xnor_1_out[5], xnor_1_out[6], xnor_1_out[7], xnor_1_out[8], xnor_1_out[9], xnor_1_out[10], xnor_1_out[11], xnor_1_out[12], xnor_1_out[13], xnor_1_out[14], xnor_1_out[15], xnor_1_out[17], xnor_1_out[18], xnor_1_out[19], xnor_1_out[20], xnor_1_out[21], xnor_1_out[22], xnor_1_out[23], xnor_1_out[24], xnor_1_out[25], xnor_1_out[26], xnor_1_out[27], xnor_1_out[28], xnor_1_out[29], xnor_1_out[30], xnor_1_out[31]);
endmodule

module taielik_liitja (
  input  A,
  input  B,
  input  C
);

  wire adder_1_cout, adder_1_out, and_1_out, and_2_out, or_1_out, xor_1_out, xor_2_out;

  xor xor_1 (xor_1_out, A, B);
  xor xor_2 (xor_2_out, xor_1_out, C);
  and and_1 (and_1_out, xor_1_out, C);
  and and_2 (and_2_out, B, A);
  Adder #(.width(1)) adder_1 (.a(B), .b(A), .out(adder_1_out), .cin(C), .cout(adder_1_cout));
  // Probe on xor_2_out
  // Probe on or_1_out
  or or_1 (or_1_out, and_1_out, and_2_out);
  // Probe on adder_1_out
  // Probe on adder_1_cout
endmodule

module Taimer (
  input  CLK,
  input  [31:0] Maluaadress,
  input  Luba_kirjutamine,
  input  lugemise_suund,
  input  [31:0] MA_kontroll,
  input  [31:0] MA_algvaartus,
  input  [31:0] MA_vordlus,
  input  [2:0] Valine_kellasisend,
  output [31:0] Valjund,
  output ulevoolu_katkestus,
  output vordlus_katkestus,
  output Puhastus,
  output valjasta_signaal
);

  wire aadressi_vordleja_1_out_3, aadressi_vordleja_2_out_3, aadressi_vordleja_3_out_3, and_1_out, and_2_out,
       and_3_out, and_4_out, and_5_out, comparator_1_lt, counter_1_carry, counter_2_carry, multiplexer_1_out,
       multiplexer_2_out, multiplexer_3_out, not_1_out, or_1_out, or_2_out;
  wire [1:0] register_1_q_2, register_1_q_3;
  wire [2:0] counter_1_q;
  wire [2:2] undriven_2;
  wire [31:0] controlled_buffer_2_out, counter_2_q, register_1_q, register_2_q, undriven;

  aadressi_vordleja aadressi_vordleja_1 (.in_1(undriven), .in_2(MA_kontroll), .out_3(aadressi_vordleja_1_out_3));
  aadressi_vordleja aadressi_vordleja_2 (.in_1(undriven), .in_2(MA_algvaartus), .out_3(aadressi_vordleja_2_out_3));
  aadressi_vordleja aadressi_vordleja_3 (.in_1(undriven), .in_2(MA_vordlus), .out_3(aadressi_vordleja_3_out_3));
  Register #(.width(32)) register_1 (
    .D({Maluaadress[31:3], undriven_2[2], Maluaadress[1:0]}), .en(and_1_out), .clk(CLK),
    .Q({register_1_q[31:9], valjasta_signaal, register_1_q_3, register_1_q[5], register_1_q_2, register_1_q[2:0]}));  // open: clr
  and and_1 (and_1_out, Luba_kirjutamine, aadressi_vordleja_1_out_3);
  and and_2 (and_2_out, Luba_kirjutamine, aadressi_vordleja_2_out_3);
  Register #(.width(32)) register_2 (.D(Maluaadress), .en(and_3_out), .clk(CLK), .Q(register_2_q));  // open: clr
  and and_3 (and_3_out, Luba_kirjutamine, aadressi_vordleja_3_out_3);
  Multiplexer #(.select(2)) multiplexer_1 (
    .in0(CLK), .in1(Valine_kellasisend[0]), .in2(Valine_kellasisend[1]), .in3(Valine_kellasisend[2]),
    .out(multiplexer_1_out), .sel(register_1_q_3));
  assign Valjund = aadressi_vordleja_1_out_3 ? {register_1_q[31:9], valjasta_signaal, register_1_q_3, register_1_q[5], register_1_q_2, register_1_q[2:0]} : 32'bz;  // Controlled_Buffer controlled_buffer_1
  assign controlled_buffer_2_out = aadressi_vordleja_2_out_3 ? counter_2_q : 32'bz;  // Controlled_Buffer controlled_buffer_2
  assign controlled_buffer_2_out = aadressi_vordleja_3_out_3 ? register_2_q : 32'bz;  // Controlled_Buffer controlled_buffer_3
  Comparator #(.mode("unsigned"), .width(32)) comparator_1 (
    .a(counter_2_q), .b(register_2_q), .lt(comparator_1_lt));  // open: gt, eq
  Counter #(.max('h7), .width(3)) counter_1 (
    .clr(or_2_out), .load(1'b0), .up(1'b1), .clk(multiplexer_1_out), .carry(counter_1_carry), .Q(counter_1_q));  // open: count, D
  not not_1 (not_1_out, comparator_1_lt);
  and and_4 (and_4_out, register_1_q[9], not_1_out);
  Multiplexer multiplexer_2 (
    .in0(register_1_q[1]), .in1(lugemise_suund), .out(multiplexer_2_out), .sel(register_1_q[5]));
  Counter #(.max('hffffffff), .width(32)) counter_2 (
    .load(and_2_out), .D(Maluaadress), .count(multiplexer_2_out), .Q(counter_2_q), .carry(counter_2_carry),
    .up(register_1_q[0]), .clk(or_2_out), .clr(or_1_out));
  or or_1 (or_1_out, and_4_out, and_5_out);
  and and_5 (and_5_out, and_1_out, register_1_q[2]);
  or or_2 (or_2_out, ~register_1_q[1], multiplexer_3_out);  // OR_Gate
  Multiplexer #(.enable("true"), .select(2)) multiplexer_3 (
    .in0(counter_1_q[0]), .in1(counter_1_q[1]), .in2(counter_1_q[2]), .in3(counter_1_carry),
    .out(multiplexer_3_out), .sel(register_1_q_2), .en(register_1_q[1]));
  and and_6 (ulevoolu_katkestus, register_1_q[5], counter_2_carry);
  and and_7 (vordlus_katkestus, register_1_q[10], and_4_out);
  or or_3 (Puhastus, counter_2_carry, or_1_out);

  // Notes on the sheet:
  //   0 - üles_alla
  //   1 - käivita
  //   2 - puhasta
  //   [3,4] - kella jagaja
  //   [6,7] - kella sisend
  //   8 - väljasta signaal
  //   9 - luba võrdlus 
  //   11 - suuna sisend
  //   5 - overflow katkestus
  //   10 - võrdluse katkestus
endmodule

module Timer_adv (
  input  [31:0] Andmed_sisse,
  input  [31:0] Malu_aadress,
  input  [31:0] TMR_ADDR,
  input  Luba_kirjutamine,
  input  [3:0] Viigud_sisse,
  input  CLK,
  output [31:0] Andmed_valja,
  output [7:0] Erandid,
  output [3:0] Viigud_valja
);

  wire aadressi_vordleja_1_out_3, aadressi_vordleja_2_out_3, aadressi_vordleja_3_out_3,
       aadressi_vordleja_4_out_3, and_1_out, and_3_out, and_4_out, and_5_out, and_6_out, and_7_out,
       and_8_out, counter_1_carry, counter_2_carry, enkooder_1_kell_valja, enkooder_1_suund,
       multiplexer_2_out, multiplexer_3_out, multiplexer_4_out, multiplexer_5_out, not_2_out,
       OCR0_kokkulangevus, OCR1_kokkulangevus, or_2_out, or_3_out, or_4_out, or_5_out, undriven;
  wire [1:0] CR_q_2;
  wire [2:0] counter_1_q;
  wire [31:0] adder_1_out, adder_2_out, adder_3_out, and_2_out, counter_2_q, CR_q, multiplexer_1_out,
       or_1_out;
  wire [31:31] not_1_out;

  Adder #(.width(32)) adder_1 (.a(TMR_ADDR), .b(32'h4), .out(adder_1_out));  // open: cin, cout
  Adder #(.width(32)) adder_2 (.a(TMR_ADDR), .b(32'h8), .out(adder_2_out));  // open: cin, cout
  Adder #(.width(32)) adder_3 (.a(TMR_ADDR), .b(32'hc), .out(adder_3_out));  // open: cin, cout
  aadressi_vordleja aadressi_vordleja_1 (.in_1(TMR_ADDR), .in_2(Malu_aadress), .out_3(aadressi_vordleja_1_out_3));
  aadressi_vordleja aadressi_vordleja_2 (.in_1(adder_1_out), .in_2(Malu_aadress), .out_3(aadressi_vordleja_2_out_3));
  aadressi_vordleja aadressi_vordleja_3 (.in_1(adder_2_out), .in_2(Malu_aadress), .out_3(aadressi_vordleja_3_out_3));
  aadressi_vordleja aadressi_vordleja_4 (.in_1(adder_3_out), .in_2(Malu_aadress), .out_3(aadressi_vordleja_4_out_3));
  and and_1 (and_1_out, aadressi_vordleja_1_out_3, Luba_kirjutamine);
  enkooder enkooder_1 (
    .A(Viigud_sisse[0]), .B(Viigud_sisse[1]), .Kell_sisse(CLK), .Suund(enkooder_1_suund),
    .Kell_valja(enkooder_1_kell_valja));
  assign or_1_out = {32{1'b0}} | {CR_q[31:3], CR_q_2, CR_q[0]};  // OR_Gate or_1, 32 bits wide
  assign and_2_out = {not_1_out[31], {31{1'b1}}} & or_1_out;  // AND_Gate and_2, 32 bits wide
  Multiplexer #(.width(32)) multiplexer_1 (
    .in0(Andmed_sisse), .in1(and_2_out), .out(multiplexer_1_out), .sel(or_5_out));
  Register #(.width(32)) CR (
    .D(multiplexer_1_out), .en(and_1_out), .clk(CLK), .Q({CR_q[31:3], CR_q_2, CR_q[0]}), .clr(undriven));
  not not_1 (not_1_out[31], or_5_out);
  assign Andmed_valja = aadressi_vordleja_1_out_3 ? {CR_q[31:3], CR_q_2, CR_q[0]} : 32'bz;  // Controlled_Buffer controlled_buffer_1
  Multiplexer #(.select(2)) multiplexer_2 (
    .in0(CLK), .in1(enkooder_1_kell_valja), .in2(Viigud_sisse[2]), .in3(Viigud_sisse[3]),
    .out(multiplexer_2_out), .sel(CR_q[4:3]));
  Counter #(.max('h7), .width(3)) counter_1 (
    .clr(or_3_out), .load(1'b0), .up(1'b1), .clk(multiplexer_2_out), .carry(counter_1_carry), .Q(counter_1_q));  // open: count, D
  // Probe on {CR_q[31:3], CR_q_2, CR_q[0]}
  and and_3 (and_3_out, Luba_kirjutamine, aadressi_vordleja_2_out_3);
  OCR OCR0 (
    .taimeri_vaartus(counter_2_q), .andmesiin_sisse(Andmed_sisse), .WE(Luba_kirjutamine),
    .RS(aadressi_vordleja_3_out_3), .CLK(CLK), .andmesiin_valja(Andmed_valja),
    .kokkulangevus(OCR0_kokkulangevus));
  OCR OCR1 (
    .taimeri_vaartus(counter_2_q), .andmesiin_sisse(Andmed_sisse), .WE(Luba_kirjutamine),
    .RS(aadressi_vordleja_4_out_3), .CLK(CLK), .andmesiin_valja(Andmed_valja),
    .kokkulangevus(OCR1_kokkulangevus));
  or or_2 (or_2_out, counter_1_carry, or_3_out);
  or or_3 (or_3_out, ~CR_q[0], multiplexer_3_out);  // OR_Gate
  Multiplexer #(.enable("true"), .select(2)) multiplexer_3 (
    .in0(counter_1_q[0]), .in1(counter_1_q[1]), .in2(counter_1_q[2]), .in3(1'b0), .out(multiplexer_3_out),
    .sel(CR_q_2), .en(CR_q[0]));
  not not_2 (not_2_out, CR_q[5]);
  Multiplexer multiplexer_4 (.in0(not_2_out), .in1(enkooder_1_suund), .out(multiplexer_4_out), .sel(CR_q[12]));
  Multiplexer multiplexer_5 (.in0(or_2_out), .in1(CLK), .out(multiplexer_5_out), .sel(and_3_out));
  and and_4 (and_4_out, CR_q[6], OCR0_kokkulangevus);
  or or_4 (or_4_out, and_4_out, and_5_out);
  and and_5 (and_5_out, CR_q[7], OCR1_kokkulangevus);
  assign Andmed_valja = aadressi_vordleja_2_out_3 ? counter_2_q : 32'bz;  // Controlled_Buffer controlled_buffer_2
  Counter #(.max('hffffffff), .width(32)) counter_2 (
    .load(and_3_out), .D(Andmed_sisse), .count(CR_q[0]), .Q(counter_2_q), .carry(counter_2_carry),
    .up(multiplexer_4_out), .clk(multiplexer_5_out), .clr(or_4_out));
  or or_5 (or_5_out, and_8_out, and_7_out, and_6_out);
  and and_6 (and_6_out, CR_q[10], counter_2_carry);
  and and_7 (and_7_out, CR_q[8], OCR0_kokkulangevus);
  and and_8 (and_8_out, CR_q[9], OCR1_kokkulangevus);
  and and_9 (Erandid[0], counter_2_carry, CR_q[31]);
  and and_10 (Erandid[1], OCR0_kokkulangevus, CR_q[29]);
  and and_11 (Erandid[2], OCR1_kokkulangevus, CR_q[30]);
  S_R_Flip_Flop #(.trigger("low")) s_r_ff_1 (
    .S(OCR0_kokkulangevus), .R(or_4_out), .clk(1'b0), .Q(Viigud_valja[0]));  // open: reset, Qn, preset
  S_R_Flip_Flop #(.trigger("low")) s_r_ff_2 (
    .S(OCR1_kokkulangevus), .R(or_4_out), .clk(1'b0), .Q(Viigud_valja[1]));  // open: reset, Qn, preset

  // Notes on the sheet:
  //   CR - Kontrollregister
  //   0 - käivita
  //   5 - üles_alla
  //   [8 - 10] - üksik
  //   [1,2] - kella jagaja
  //   [3,4] - kella sisend
  //   [6,7] - OCR_lähtestus
  //   12 - enkoodri suuna valik
  //   29 - OCR0_võrdluskatkestus
  //   30 - OCR1_võrdluskatkestus
  //   31 - ülevoolukatkestus
endmodule

module OCR (
  input  [31:0] taimeri_vaartus,
  input  [31:0] andmesiin_sisse,
  input  WE,
  input  RS,
  input  CLK,
  output kokkulangevus,
  output [31:0] andmesiin_valja
);

  wire and_1_out;
  wire [31:0] register_1_q;

  and and_1 (and_1_out, WE, RS);
  Register #(.width(32)) register_1 (.D(andmesiin_sisse), .en(and_1_out), .clk(CLK), .Q(register_1_q));  // open: clr
  assign andmesiin_valja = RS ? register_1_q : 32'bz;  // Controlled_Buffer controlled_buffer_1
  Comparator #(.mode("unsigned"), .width(32)) comparator_1 (
    .a(taimeri_vaartus), .b(register_1_q), .eq(kokkulangevus));  // open: gt, lt
endmodule

module enkooder (
  input  A,
  input  B,
  input  Kell_sisse,
  output Suund,
  output Kell_valja
);

  wire and_1_out, and_2_out, and_3_out, and_4_out, and_5_out, and_6_out, and_7_out, and_8_out, d_ff_1_q,
       d_ff_2_q, Eelmine_A_q, Eelmine_B_q, or_2_out, or_3_out;

  D_Flip_Flop d_ff_1 (.D(A), .clk(Kell_sisse), .Q(d_ff_1_q));  // open: Qn, preset, reset
  D_Flip_Flop d_ff_2 (.D(B), .clk(Kell_sisse), .Q(d_ff_2_q));  // open: Qn, preset, reset
  D_Flip_Flop Eelmine_A (.D(d_ff_1_q), .clk(Kell_sisse), .Q(Eelmine_A_q));  // open: Qn, preset, reset
  D_Flip_Flop Eelmine_B (.D(d_ff_2_q), .clk(Kell_sisse), .Q(Eelmine_B_q));  // open: Qn, preset, reset
  and and_1 (and_1_out, d_ff_1_q, ~d_ff_2_q, ~Eelmine_A_q, ~Eelmine_B_q);  // AND_Gate
  and and_2 (and_2_out, d_ff_1_q, d_ff_2_q, Eelmine_A_q, ~Eelmine_B_q);  // AND_Gate
  and and_3 (and_3_out, ~d_ff_1_q, d_ff_2_q, Eelmine_A_q, Eelmine_B_q);  // AND_Gate
  and and_4 (and_4_out, ~d_ff_1_q, ~d_ff_2_q, ~Eelmine_A_q, Eelmine_B_q);  // AND_Gate
  and and_5 (and_5_out, ~d_ff_1_q, d_ff_2_q, ~Eelmine_A_q, ~Eelmine_B_q);  // AND_Gate
  and and_6 (and_6_out, d_ff_1_q, d_ff_2_q, ~Eelmine_A_q, Eelmine_B_q);  // AND_Gate
  and and_7 (and_7_out, d_ff_1_q, ~d_ff_2_q, Eelmine_A_q, Eelmine_B_q);  // AND_Gate
  and and_8 (and_8_out, ~d_ff_1_q, ~d_ff_2_q, Eelmine_A_q, ~Eelmine_B_q);  // AND_Gate
  or or_1 (Suund, and_1_out, and_2_out, and_3_out, and_4_out);
  or or_2 (or_2_out, and_5_out, and_6_out, and_7_out, and_8_out);
  or or_3 (or_3_out, Suund, or_2_out);
  and and_9 (Kell_valja, or_3_out, ~Kell_sisse);  // AND_Gate
endmodule
